// Logisim project 16位全加器.circ as structural Verilog
module \半加器  (
  input  in_1,
  input  in_2,
  output out_3,
  output out_4
);

  and and_1 (out_3, in_1, in_2);
  xor xor_1 (out_4, in_1, in_2);
endmodule

module \_4位全加器  (
  input  [3:0] in_1,
  input  [3:0] in_2,
  input  in_3,
  output [3:0] out_4,
  output out_5
);

  wire \n1位全加器_1_co , \n1位全加器_2_co , \n1位全加器_3_co ;

  \_1位全加器  \u_1位全加器_1  (.A(in_1[0]), .B(in_2[0]), .Ci(in_3), .Co(\n1位全加器_1_co ), .S(out_4[0]));
  \_1位全加器  \u_1位全加器_2  (.A(in_1[1]), .B(in_2[1]), .Ci(\n1位全加器_1_co ), .Co(\n1位全加器_2_co ), .S(out_4[1]));
  \_1位全加器  \u_1位全加器_3  (.A(in_1[2]), .B(in_2[2]), .Ci(\n1位全加器_2_co ), .Co(\n1位全加器_3_co ), .S(out_4[2]));
  \_1位全加器  \u_1位全加器_4  (.A(in_1[3]), .B(in_2[3]), .Ci(\n1位全加器_3_co ), .Co(out_5), .S(out_4[3]));
endmodule

module \_1位全加器  (
  input  A,
  input  B,
  input  Ci,
  output Co,
  output S
);

  wire \半加器_1_out_3 , \半加器_1_out_4 , \半加器_2_out_3 ;

  \半加器  \u_半加器_1  (.in_1(A), .in_2(B), .out_3(\半加器_1_out_3 ), .out_4(\半加器_1_out_4 ));
  \半加器  \u_半加器_2  (.in_1(\半加器_1_out_4 ), .in_2(Ci), .out_3(\半加器_2_out_3 ), .out_4(S));
  or or_1 (Co, \半加器_2_out_3 , \半加器_1_out_3 );
endmodule

module \_16位全加器  (
  input  [15:0] in_1,
  input  [15:0] in_2,
  input  in_3,
  output [15:0] out_4,
  output out_5
);

  wire \n4位全加器_1_out_5 , \n4位全加器_2_out_5 , \n4位全加器_3_out_5 ;

  \_4位全加器  \u_4位全加器_1  (.in_1(in_1[3:0]), .in_2(in_2[3:0]), .in_3(in_3), .out_4(out_4[3:0]), .out_5(\n4位全加器_1_out_5 ));
  \_4位全加器  \u_4位全加器_2  (
    .in_1(in_1[7:4]), .in_2(in_2[7:4]), .in_3(\n4位全加器_1_out_5 ), .out_4(out_4[7:4]), .out_5(\n4位全加器_2_out_5 ));
  \_4位全加器  \u_4位全加器_3  (
    .in_1(in_1[11:8]), .in_2(in_2[11:8]), .in_3(\n4位全加器_2_out_5 ), .out_4(out_4[11:8]),
    .out_5(\n4位全加器_3_out_5 ));
  \_4位全加器  \u_4位全加器_4  (
    .in_1(in_1[15:12]), .in_2(in_2[15:12]), .in_3(\n4位全加器_3_out_5 ), .out_4(out_4[15:12]), .out_5(out_5));
endmodule

module \_32位全加器  (
  input  [31:0] in_1,
  input  [31:0] in_2,
  input  in_3,
  output [31:0] out_4,
  output out_5
);

  wire \n16位全加器_1_out_5 ;

  \_16位全加器  \u_16位全加器_1  (
    .in_1(in_1[15:0]), .in_2(in_2[15:0]), .in_3(in_3), .out_4(out_4[15:0]), .out_5(\n16位全加器_1_out_5 ));
  \_16位全加器  \u_16位全加器_2  (
    .in_1(in_1[31:16]), .in_2(in_2[31:16]), .in_3(\n16位全加器_1_out_5 ), .out_4(out_4[31:16]), .out_5(out_5));
endmodule

module \_32位ALU  (
  input  [3:0] OP,
  input  [31:0] A,
  input  [31:0] B,
  input  in_4,
  input  [31:0] in_5,
  input  [30:0] in_6,
  output [31:0] out_7
);

  wire [0:0] comparator_1_lt;
  wire [31:0] and_1_out, divider_1_out, multiplier_1_out, \n32位全加器_1_out_4 , nor_1_out, or_1_out,
       shifter_1_out, subtractor_1_out, xor_1_out;

  assign and_1_out = A & B;  // AND_Gate and_1, 32 bits wide
  assign or_1_out = A | B;  // OR_Gate or_1, 32 bits wide
  \_32位全加器  \u_32位全加器_1  (.in_1(A), .in_2(B), .in_3(in_4), .out_4(\n32位全加器_1_out_4 ));  // open: out_5
  assign xor_1_out = A ^ B;  // XOR_Gate xor_1, 32 bits wide
  assign nor_1_out = ~(A | B);  // NOR_Gate nor_1, 32 bits wide
  Subtractor #(.width(32)) subtractor_1 (.a(A), .b(B), .out(subtractor_1_out), .bin(in_4));  // open: bout
  Multiplier #(.width(32)) multiplier_1 (.a(A), .b(B), .out(multiplier_1_out), .cin(in_5));  // open: cout
  Divider #(.width(32)) divider_1 (.a(A), .b(B), .out(divider_1_out), .upper(in_5));  // open: rem
  Comparator #(.width(32), .mode("unsigned")) comparator_1 (.a(A), .b(B), .lt(comparator_1_lt[0]));  // open: gt, eq
  Shifter #(.width(32), .shift("ll")) shifter_1 (.in(A), .\dist (B[4:0]), .out(shifter_1_out));
  Multiplexer #(.select(4), .width(32), .disabled("Z"), .enable("false")) multiplexer_1 (
    .in0(and_1_out), .in1(or_1_out), .in2(xor_1_out), .in3(nor_1_out), .in4(\n32位全加器_1_out_4 ),
    .in5(subtractor_1_out), .in6(multiplier_1_out), .in7(divider_1_out), .in8({in_6, comparator_1_lt[0]}),
    .in9(shifter_1_out), .out(out_7), .sel(OP));  // open: in10, in11, in12, in13, in14, in15
endmodule
