// Logisim project RAM.circ as structural Verilog: 1 circuit, main circuit main
module main (
  input  [7:0] in_1,
  input  [31:0] in_2,
  input  in_3,
  output [31:0] out_4
);

  wire clock_1_out;

  Clock #(.highDuration(1), .lowDuration(1)) clock_1 (.out(clock_1_out));
  RAM #(.addrWidth(8), .dataWidth(32), .bus("separate"), .Select("low")) ram_1 (
    .addr(in_1), .din(in_2), .data(out_4), .clk(clock_1_out), .ld(in_3));  // open: str, sel, clr
endmodule
