// Logisim project RF.circ as structural Verilog
module RF10 (
  input  WE3,
  input  [3:0] W_Reg,
  input  [3:0] R_Reg,
  input  [31:0] W_data,
  output [31:0] R_data
);

  wire clock_1_out, decoder_1_out0, decoder_1_out1, decoder_1_out2, decoder_1_out3, decoder_1_out4,
       decoder_1_out5, decoder_1_out6, decoder_1_out7, decoder_1_out8, decoder_1_out9;
  wire [31:0] register_1_q, register_2_q, register_3_q, register_4_q, register_5_q, register_6_q,
       register_7_q, register_8_q, register_9_q, register_10_q;

  Decoder #(.select(4), .tristate("false"), .disabled("Z"), .enable("true")) decoder_1 (
    .out0(decoder_1_out0), .out1(decoder_1_out1), .out2(decoder_1_out2), .out3(decoder_1_out3),
    .out4(decoder_1_out4), .out5(decoder_1_out5), .out6(decoder_1_out6), .out7(decoder_1_out7),
    .out8(decoder_1_out8), .out9(decoder_1_out9), .sel(W_Reg), .en(WE3));  // open: out10, out11, out12, out13, out14, out15
  Clock #(.highDuration(1), .lowDuration(1)) clock_1 (.out(clock_1_out));
  Register #(.width(32), .trigger("rising"), .Select("low")) register_1 (
    .D(W_data), .en(decoder_1_out0), .Q(register_1_q), .clk(clock_1_out));  // open: clr
  Register #(.width(32), .trigger("rising"), .Select("low")) register_2 (
    .D(W_data), .en(decoder_1_out1), .Q(register_2_q), .clk(clock_1_out));  // open: clr
  Register #(.width(32), .trigger("rising"), .Select("low")) register_3 (
    .D(W_data), .en(decoder_1_out2), .Q(register_3_q), .clk(clock_1_out));  // open: clr
  Register #(.width(32), .trigger("rising"), .Select("low")) register_4 (
    .D(W_data), .en(decoder_1_out3), .Q(register_4_q), .clk(clock_1_out));  // open: clr
  Register #(.width(32), .trigger("rising"), .Select("low")) register_5 (
    .D(W_data), .en(decoder_1_out4), .Q(register_5_q), .clk(clock_1_out));  // open: clr
  Register #(.width(32), .trigger("rising"), .Select("low")) register_6 (
    .D(W_data), .en(decoder_1_out5), .Q(register_6_q), .clk(clock_1_out));  // open: clr
  Register #(.width(32), .trigger("rising"), .Select("low")) register_7 (
    .D(W_data), .en(decoder_1_out6), .Q(register_7_q), .clk(clock_1_out));  // open: clr
  Register #(.width(32), .trigger("rising"), .Select("low")) register_8 (
    .D(W_data), .en(decoder_1_out7), .Q(register_8_q), .clk(clock_1_out));  // open: clr
  Register #(.width(32), .trigger("rising"), .Select("low")) register_9 (
    .D(W_data), .en(decoder_1_out8), .Q(register_9_q), .clk(clock_1_out));  // open: clr
  Register #(.width(32), .trigger("rising"), .Select("low")) register_10 (
    .D(W_data), .en(decoder_1_out9), .Q(register_10_q), .clk(clock_1_out));  // open: clr
  Multiplexer #(.select(4), .width(32), .disabled("Z"), .enable("false")) multiplexer_1 (
    .in0(register_1_q), .in1(register_2_q), .in2(register_3_q), .in3(register_4_q), .in4(register_5_q),
    .in5(register_6_q), .in6(register_7_q), .in7(register_8_q), .in8(register_9_q), .in9(register_10_q),
    .out(R_data), .sel(R_Reg));  // open: in10, in11, in12, in13, in14, in15
endmodule
