// Logisim project Work1.circ as structural Verilog: 1 circuit, main circuit main
module main (
  input  in_1,
  input  in_2,
  input  in_3,
  input  in_4,
  input  A,
  input  B,
  input  ENABLE,
  output out_8,
  output x_OR_y,
  output Z_0,
  output Z_1,
  output Z_2,
  output Z_3
);

  wire and_2_out, and_3_out, not_1_out, not_2_out, not_3_out, not_4_out;

  not not_1 (not_1_out, A);
  not not_2 (not_2_out, B);
  not not_3 (not_3_out, in_3);
  not not_4 (not_4_out, in_4);
  and and_1 (out_8, in_1, in_2);
  and and_2 (and_2_out, not_3_out, in_4);
  and and_3 (and_3_out, in_3, not_4_out);
  or or_1 (x_OR_y, and_2_out, and_3_out);
  nand nand_1 (Z_0, not_1_out, ENABLE, not_2_out);
  nand nand_2 (Z_1, not_1_out, B, ENABLE);
  nand nand_3 (Z_2, A, not_2_out, ENABLE);
  nand nand_4 (Z_3, B, A, ENABLE);
endmodule
