// Logisim project 0c7a52ec.circ as structural Verilog: 11 circuits, main circuit 10寄存器CPU
module \_10寄存器CPU  (
  output RegWrite,
  output MemWrite,
  output [31:0] PC,
  output [31:0] IR,
  output [31:0] RDin,
  output [31:0] MDin
);

  wire alu_1_equal, and_1_out, and_2_out, CLK, clock_1_out, clock_2_out, clock_4_out, clock_5_out, Halt,
       not_1_out, not_2_out, not_3_out, or_1_out, RST, \单周期cpu控制器_1_alusrc , \单周期cpu控制器_1_beq ,
       \单周期cpu控制器_1_bne , \单周期cpu控制器_1_j , \单周期cpu控制器_1_memtoreg1 , \单周期cpu控制器_1_memtoreg2 ,
       \单周期cpu控制器_1_regdst ;
  wire [3:0] multiplexer_3_out, \单周期cpu控制器_1_alu_op ;
  wire [15:0] \总周期数 ;
  wire [31:0] adder_1_out, adder_2_out, alu_1_result, bit_extender_1_out, multiplexer_1_out,
       multiplexer_2_out, multiplexer_4_out, multiplexer_5_out, ram_1_data, rf10_1_rd1, shifter_1_out;

  not not_1 (not_1_out, Halt);
  Counter #(.width(16), .max('hffff), .ongoal("wrap"), .trigger("rising"), .behavior("old")) counter_1 (
    .count(not_1_out), .Q(\总周期数 ), .clk(clock_1_out), .clr(RST));  // open: load, D, carry, preset
  Clock #(.highDuration(1), .lowDuration(1)) clock_1 (.out(clock_1_out));
  Button \u_总复位  (.out(RST));
  Multiplexer #(.select(1), .width(32), .disabled("Z"), .enable("false")) multiplexer_1 (
    .in0(adder_1_out), .in1(adder_2_out), .out(multiplexer_1_out), .sel(or_1_out));
  Multiplexer #(.select(1), .width(32), .disabled("Z"), .enable("false")) multiplexer_2 (
    .in0(multiplexer_1_out), .in1({adder_1_out[31:28], IR[25:0], 2'b00}), .out(multiplexer_2_out),
    .sel(\单周期cpu控制器_1_j ));
  Register #(.width(32), .trigger("rising"), .Select("low")) u_PC (
    .D(multiplexer_2_out), .en(not_2_out), .Q(PC), .clk(clock_2_out), .clr(RST));
  Clock #(.highDuration(1), .lowDuration(1)) clock_2 (.out(clock_2_out));
  not not_2 (not_2_out, Halt);
  Clock #(.highDuration(1), .lowDuration(1)) clock_3 (.out(CLK));
  Adder #(.width(32)) adder_1 (.a(PC), .b(32'h4), .out(adder_1_out));  // open: cin, cout
  // Probe on IR[31:26]
  // Probe on \总周期数 
  // Probe on \总周期数 
  ROM #(.addrWidth(10), .dataWidth(32), .Select("high")) rom_1 (.addr(PC[11:2]), .data(IR));
  \单周期CPU控制器  \u_单周期cpu控制器_1  (
    .Func(IR[5:0]), .RegWrite(RegWrite), .MemToReg1(\单周期cpu控制器_1_memtoreg1 ), .MemWrite(MemWrite),
    .Beq(\单周期cpu控制器_1_beq ), .Bne(\单周期cpu控制器_1_bne ), .RegDst(\单周期cpu控制器_1_regdst ),
    .AluSrc(\单周期cpu控制器_1_alusrc ), .ALU_OP(\单周期cpu控制器_1_alu_op ), .OP(IR[31:26]), .Halt(Halt),
    .MemToReg2(\单周期cpu控制器_1_memtoreg2 ), .in_3(1'b1), .J(\单周期cpu控制器_1_j ));
  // Probe on IR[5:0]
  Multiplexer #(.select(1), .width(4), .disabled("Z"), .enable("false")) multiplexer_3 (
    .in0(IR[19:16]), .in1(IR[14:11]), .out(multiplexer_3_out), .sel(\单周期cpu控制器_1_regdst ));
  RF10 rf10_1 (
    .WE3(RegWrite), .A3(multiplexer_3_out), .A1(IR[24:21]), .WD(RDin), .A2(IR[19:16]), .RD1(rf10_1_rd1),
    .RD2(MDin), .in_1(clock_4_out));
  Clock #(.highDuration(1), .lowDuration(1)) clock_4 (.out(clock_4_out));
  assign bit_extender_1_out = {{16{IR[15]}}, IR[15:0]};  // Bit_Extender bit_extender_1
  // Probe on \单周期cpu控制器_1_alu_op 
  Multiplexer #(.select(1), .width(32), .disabled("Z"), .enable("false")) multiplexer_4 (
    .in0(MDin), .in1(bit_extender_1_out), .out(multiplexer_4_out), .sel(\单周期cpu控制器_1_alusrc ));
  Shifter #(.width(32), .shift("ll")) shifter_1 (.in(bit_extender_1_out), .\dist (5'b00010), .out(shifter_1_out));
  ALU alu_1 (
    .X(rf10_1_rd1), .Y(multiplexer_4_out), .AluOP(\单周期cpu控制器_1_alu_op ), .Equal(alu_1_equal),
    .Result(alu_1_result));  // open: Result_2
  Adder #(.width(32)) adder_2 (.a(shifter_1_out), .b(adder_1_out), .out(adder_2_out));  // open: cin, cout
  and and_1 (and_1_out, \单周期cpu控制器_1_beq , alu_1_equal);
  and and_2 (and_2_out, \单周期cpu控制器_1_bne , not_3_out);
  not not_3 (not_3_out, alu_1_equal);
  or or_1 (or_1_out, and_1_out, and_2_out);
  Clock #(.highDuration(1), .lowDuration(1)) clock_5 (.out(clock_5_out));
  RAM #(.addrWidth(10), .dataWidth(32), .bus("separate"), .Select("high")) ram_1 (
    .addr(alu_1_result[11:2]), .din(MDin), .data(ram_1_data), .str(MemWrite), .clk(clock_5_out), .clr(RST));  // open: sel, ld
  Multiplexer #(.select(1), .width(32), .disabled("Z"), .enable("false")) multiplexer_5 (
    .in0(alu_1_result), .in1(ram_1_data), .out(multiplexer_5_out), .sel(\单周期cpu控制器_1_memtoreg1 ));
  Multiplexer #(.select(1), .width(32), .disabled("Z"), .enable("false")) multiplexer_6 (
    .in0(multiplexer_5_out), .in1({IR[15:0], {16{1'b0}}}), .out(RDin), .sel(\单周期cpu控制器_1_memtoreg2 ));

  // Notes on the sheet:
  //   PC+4
  //   程序运行结束后可停机，查看数据存储器中80单元的排序情况是有符号降序
  //   总周期数参考值：224
  //   指令存储器
  //   PC+4
  //   rs
  //   contents of rom_1 (hex, n*v repeats v):
  //   3c0155aa 2002000a c
  //   rt
  //   rd
  //   MemtoReg1
  //   MemWrite
  //   Beq
  //   Bne
  //   AluOP
  //   AluSrc
  //   RegWrite
  //   RegDst
  //   MemtoReg2
  //   为方便自动评测，需要输出PC，IR，寄存器文件写入端口RDin，内存写入端口MDin等信号
  //   数据存储器
endmodule

module \_32寄存器CPU  (
  output RegWrite,
  output MemWrite,
  output [31:0] PC,
  output [31:0] IR,
  output [31:0] RDin,
  output [31:0] MDin
);

  wire alu_1_equal, and_1_out, and_2_out, CLK, clock_1_out, clock_2_out, clock_4_out, clock_5_out, Halt,
       not_1_out, not_2_out, not_3_out, or_1_out, RST, \单周期cpu控制器_1_alusrc , \单周期cpu控制器_1_beq ,
       \单周期cpu控制器_1_bne , \单周期cpu控制器_1_j , \单周期cpu控制器_1_memtoreg1 , \单周期cpu控制器_1_memtoreg2 ,
       \单周期cpu控制器_1_regdst ;
  wire [3:0] adder_1_out, \单周期cpu控制器_1_alu_op ;
  wire [4:0] multiplexer_3_out;
  wire [15:0] \总周期数 ;
  wire [27:0] adder_1_out_2;
  wire [31:0] adder_2_out, alu_1_result, bit_extender_1_out, multiplexer_1_out, multiplexer_2_out,
       multiplexer_4_out, multiplexer_5_out, ram_1_data, regifile_1_r1, shifter_1_out;

  not not_1 (not_1_out, Halt);
  Counter #(.width(16), .max('hffff), .ongoal("wrap"), .trigger("rising"), .behavior("old")) counter_1 (
    .count(not_1_out), .Q(\总周期数 ), .clk(clock_1_out), .clr(RST));  // open: load, D, carry, preset
  Clock #(.highDuration(1), .lowDuration(1)) clock_1 (.out(clock_1_out));
  Button \u_总复位  (.out(RST));
  Multiplexer #(.select(1), .width(32), .disabled("Z"), .enable("false")) multiplexer_1 (
    .in0({adder_1_out, adder_1_out_2}), .in1(adder_2_out), .out(multiplexer_1_out), .sel(or_1_out));
  Multiplexer #(.select(1), .width(32), .disabled("Z"), .enable("false")) multiplexer_2 (
    .in0(multiplexer_1_out), .in1({adder_1_out, IR[25:0], 2'b00}), .out(multiplexer_2_out),
    .sel(\单周期cpu控制器_1_j ));
  Register #(.width(32), .trigger("rising"), .Select("low")) u_PC (
    .D(multiplexer_2_out), .en(not_2_out), .Q(PC), .clk(clock_2_out), .clr(RST));
  Clock #(.highDuration(1), .lowDuration(1)) clock_2 (.out(clock_2_out));
  not not_2 (not_2_out, Halt);
  Clock #(.highDuration(1), .lowDuration(1)) clock_3 (.out(CLK));
  Adder #(.width(32)) adder_1 (.a(PC), .b(32'h4), .out({adder_1_out, adder_1_out_2}));  // open: cin, cout
  // Probe on IR[31:26]
  // Probe on \总周期数 
  // Probe on \总周期数 
  ROM #(.addrWidth(10), .dataWidth(32), .Select("high")) rom_1 (.addr(PC[11:2]), .data(IR));
  \单周期CPU控制器  \u_单周期cpu控制器_1  (
    .Func(IR[5:0]), .RegWrite(RegWrite), .MemToReg1(\单周期cpu控制器_1_memtoreg1 ), .MemWrite(MemWrite),
    .Beq(\单周期cpu控制器_1_beq ), .Bne(\单周期cpu控制器_1_bne ), .RegDst(\单周期cpu控制器_1_regdst ),
    .AluSrc(\单周期cpu控制器_1_alusrc ), .ALU_OP(\单周期cpu控制器_1_alu_op ), .OP(IR[31:26]), .Halt(Halt),
    .MemToReg2(\单周期cpu控制器_1_memtoreg2 ), .in_3(1'b1), .J(\单周期cpu控制器_1_j ));
  // Probe on IR[5:0]
  Multiplexer #(.select(1), .width(5), .disabled("Z"), .enable("false")) multiplexer_3 (
    .in0(IR[20:16]), .in1(IR[15:11]), .out(multiplexer_3_out), .sel(\单周期cpu控制器_1_regdst ));
  RegiFile regifile_1 (
    .Din(RDin), .Clk(clock_4_out), .R1(regifile_1_r1), .R2(MDin), .WE(RegWrite), .W_num(multiplexer_3_out),
    .R1_num(IR[25:21]), .R2_num(IR[20:16]));
  Clock #(.highDuration(1), .lowDuration(1)) clock_4 (.out(clock_4_out));
  assign bit_extender_1_out = {{16{IR[15]}}, IR[15:0]};  // Bit_Extender bit_extender_1
  // Probe on \单周期cpu控制器_1_alu_op 
  Multiplexer #(.select(1), .width(32), .disabled("Z"), .enable("false")) multiplexer_4 (
    .in0(MDin), .in1(bit_extender_1_out), .out(multiplexer_4_out), .sel(\单周期cpu控制器_1_alusrc ));
  Shifter #(.width(32), .shift("ll")) shifter_1 (.in(bit_extender_1_out), .\dist (5'b00010), .out(shifter_1_out));
  ALU alu_1 (
    .X(regifile_1_r1), .Y(multiplexer_4_out), .AluOP(\单周期cpu控制器_1_alu_op ), .Equal(alu_1_equal),
    .Result(alu_1_result));  // open: Result_2
  Adder #(.width(32)) adder_2 (
    .a(shifter_1_out), .b({adder_1_out, adder_1_out_2}), .out(adder_2_out));  // open: cin, cout
  and and_1 (and_1_out, \单周期cpu控制器_1_beq , alu_1_equal);
  and and_2 (and_2_out, \单周期cpu控制器_1_bne , not_3_out);
  not not_3 (not_3_out, alu_1_equal);
  or or_1 (or_1_out, and_1_out, and_2_out);
  Clock #(.highDuration(1), .lowDuration(1)) clock_5 (.out(clock_5_out));
  RAM #(.addrWidth(10), .dataWidth(32), .bus("separate"), .Select("high")) ram_1 (
    .addr(alu_1_result[11:2]), .din(MDin), .data(ram_1_data), .str(MemWrite), .clk(clock_5_out), .clr(RST));  // open: sel, ld
  Multiplexer #(.select(1), .width(32), .disabled("Z"), .enable("false")) multiplexer_5 (
    .in0(alu_1_result), .in1(ram_1_data), .out(multiplexer_5_out), .sel(\单周期cpu控制器_1_memtoreg1 ));
  Multiplexer #(.select(1), .width(32), .disabled("Z"), .enable("false")) multiplexer_6 (
    .in0(multiplexer_5_out), .in1({IR[15:0], {16{1'b0}}}), .out(RDin), .sel(\单周期cpu控制器_1_memtoreg2 ));

  // Notes on the sheet:
  //   PC+4
  //   程序运行结束后可停机，查看数据存储器中80单元的排序情况是有符号降序
  //   总周期数参考值：224
  //   指令存储器
  //   PC+4
  //   rs
  //   contents of rom_1 (hex, n*v repeats v):
  //   3c0155aa 2002000a c
  //   rt
  //   rd
  //   MemtoReg1
  //   MemWrite
  //   Beq
  //   Bne
  //   AluOP
  //   AluSrc
  //   RegWrite
  //   RegDst
  //   MemtoReg2
  //   为方便自动评测，需要输出PC，IR，寄存器文件写入端口RDin，内存写入端口MDin等信号
  //   数据存储器
endmodule

// 单周期硬布线控制器
module \单周期CPU控制器  (
  input  [5:0] OP,
  input  [5:0] Func,
  input  in_3,
  output [3:0] ALU_OP,
  output MemToReg1,
  output AluSrc,
  output Beq,
  output Bne,
  output Halt,
  output RegWrite,
  output MemWrite,
  output J,
  output MemToReg2,
  output RegDst
);

  wire ADD, ADDI, ADDIU, ADDU, AND, and_1_out, ANDI, comparator_6_eq, comparator_23_eq, comparator_24_eq,
       comparator_25_eq, comparator_26_eq, comparator_27_eq, comparator_28_eq, comparator_29_eq,
       comparator_30_eq, comparator_31_eq, comparator_32_eq, LB, LBU, LH, LHU, LW, NOR, not_1_out, not_2_out,
       not_3_out, not_4_out, not_5_out, not_6_out, OR, or_1_out, or_2_out, or_3_out, or_4_out, or_5_out,
       or_6_out, or_10_out, or_11_out, or_12_out, or_15_out, ORI, R_TYPE, SB, SH, SLT, SLTI, SLTIU, SUB,
       SUBU, SW, XOR;

  // Probe on OP
  or or_1 (or_1_out, SLTIU, SLTI);
  or or_2 (or_2_out, LH, LBU, LB, LHU);
  or or_3 (or_3_out, SUBU, SUB);
  or or_4 (or_4_out, ADDI, ADDIU);
  or or_5 (or_5_out, SH, SB);
  not not_1 (not_1_out, SLT);
  not not_2 (not_2_out, XOR);
  not not_3 (not_3_out, AND);
  not not_4 (not_4_out, OR);
  and and_1 (and_1_out, not_2_out, not_4_out, R_TYPE, not_5_out, not_3_out, not_1_out);
  Comparator #(.width(6), .mode("twosComplement")) comparator_1 (.a(OP), .b(6'b100011), .eq(LW));  // open: gt, lt
  Comparator #(.width(6), .mode("twosComplement")) comparator_2 (.a(OP), .b(6'b101011), .eq(SW));  // open: gt, lt
  Comparator #(.width(6), .mode("twosComplement")) comparator_3 (.a(OP), .b(6'b000100), .eq(Beq));  // open: gt, lt
  Comparator #(.width(6), .mode("twosComplement")) comparator_4 (.a(OP), .b(6'b000101), .eq(Bne));  // open: gt, lt
  Comparator #(.width(6), .mode("twosComplement")) comparator_5 (.a(OP), .b(6'b001000), .eq(ADDI));  // open: gt, lt
  Comparator #(.width(6), .mode("twosComplement")) comparator_6 (
    .a(OP), .b({6{1'b0}}), .eq(comparator_6_eq));  // open: gt, lt
  Comparator #(.width(6), .mode("twosComplement")) comparator_7 (.a(OP), .b(6'b001101), .eq(ORI));  // open: gt, lt
  Comparator #(.width(6), .mode("twosComplement")) comparator_8 (
    .a(OP), .b(6'b001111), .eq(MemToReg2));  // open: gt, lt
  Comparator #(.width(6), .mode("twosComplement")) comparator_9 (.a(OP), .b(6'b100000), .eq(LB));  // open: gt, lt
  Comparator #(.width(6), .mode("twosComplement")) comparator_10 (.a(OP), .b(6'b100100), .eq(LBU));  // open: gt, lt
  Comparator #(.width(6), .mode("twosComplement")) comparator_11 (.a(OP), .b(6'b100001), .eq(LH));  // open: gt, lt
  Comparator #(.width(6), .mode("twosComplement")) comparator_12 (.a(OP), .b(6'b100101), .eq(LHU));  // open: gt, lt
  Comparator #(.width(6), .mode("twosComplement")) comparator_13 (.a(OP), .b(6'b101000), .eq(SB));  // open: gt, lt
  Comparator #(.width(6), .mode("twosComplement")) comparator_14 (.a(OP), .b(6'b101001), .eq(SH));  // open: gt, lt
  Comparator #(.width(6), .mode("twosComplement")) comparator_15 (.a(OP), .b(6'b001001), .eq(ADDIU));  // open: gt, lt
  Comparator #(.width(6), .mode("twosComplement")) comparator_16 (.a(OP), .b(6'b001100), .eq(ANDI));  // open: gt, lt
  Comparator #(.width(6), .mode("twosComplement")) comparator_17 (.a(OP), .b(6'b001101), .eq(ORI));  // open: gt, lt
  Comparator #(.width(6), .mode("twosComplement")) comparator_18 (.a(OP), .b(6'b001110), .eq(XOR));  // open: gt, lt
  Comparator #(.width(6), .mode("twosComplement")) comparator_19 (.a(OP), .b(6'b001010), .eq(SLTI));  // open: gt, lt
  Comparator #(.width(6), .mode("twosComplement")) comparator_20 (.a(OP), .b(6'b001011), .eq(SLTIU));  // open: gt, lt
  Comparator #(.width(6), .mode("twosComplement")) comparator_21 (.a(OP), .b(6'b000010), .eq(J));  // open: gt, lt
  Comparator #(.width(16), .mode("twosComplement")) comparator_22 ();  // open: a, b, gt, eq, lt
  not not_5 (not_5_out, or_3_out);
  or or_6 (or_6_out, or_4_out, and_1_out, or_2_out, or_5_out, SW);
  Comparator #(.width(6), .mode("twosComplement")) comparator_23 (
    .a(Func), .b(6'b100000), .eq(comparator_23_eq));  // open: gt, lt
  Comparator #(.width(6), .mode("twosComplement")) comparator_24 (
    .a(Func), .b(6'b101010), .eq(comparator_24_eq));  // open: gt, lt
  Comparator #(.width(6), .mode("twosComplement")) comparator_25 (
    .a(Func), .b(6'b001100), .eq(comparator_25_eq));  // open: gt, lt
  Comparator #(.width(6), .mode("twosComplement")) comparator_26 (
    .a(Func), .b(6'b100001), .eq(comparator_26_eq));  // open: gt, lt
  Comparator #(.width(6), .mode("twosComplement")) comparator_27 (
    .a(Func), .b(6'b100011), .eq(comparator_27_eq));  // open: gt, lt
  Comparator #(.width(6), .mode("twosComplement")) comparator_28 (
    .a(Func), .b(6'b100010), .eq(comparator_28_eq));  // open: gt, lt
  Comparator #(.width(6), .mode("twosComplement")) comparator_29 (
    .a(Func), .b(6'b100100), .eq(comparator_29_eq));  // open: gt, lt
  Comparator #(.width(6), .mode("twosComplement")) comparator_30 (
    .a(Func), .b(6'b100101), .eq(comparator_30_eq));  // open: gt, lt
  Comparator #(.width(6), .mode("twosComplement")) comparator_31 (
    .a(Func), .b(6'b100110), .eq(comparator_31_eq));  // open: gt, lt
  Comparator #(.width(6), .mode("twosComplement")) comparator_32 (
    .a(Func), .b(6'b100111), .eq(comparator_32_eq));  // open: gt, lt
  and and_2 (ADD, comparator_23_eq, comparator_6_eq);
  and and_3 (SLT, comparator_24_eq, comparator_6_eq);
  and and_4 (Halt, comparator_25_eq, comparator_6_eq);
  and and_5 (ADDU, comparator_26_eq, comparator_6_eq);
  and and_6 (SUBU, comparator_27_eq, comparator_6_eq);
  and and_7 (SUB, comparator_28_eq, comparator_6_eq);
  and and_8 (AND, comparator_29_eq, comparator_6_eq);
  and and_9 (OR, comparator_30_eq, comparator_6_eq);
  and and_10 (XOR, comparator_31_eq, comparator_6_eq);
  and and_11 (NOR, comparator_32_eq, comparator_6_eq);
  or or_7 (MemToReg1, or_2_out, LW);
  or or_8 (MemWrite, SW, or_5_out);
  or or_9 (AluSrc, or_1_out, ORI, or_5_out, LW, ORI, or_4_out, or_2_out, SW, ANDI, XOR);
  or or_10 (or_10_out, ANDI, AND);
  or or_11 (or_11_out, OR, ORI, ORI);
  or or_12 (or_12_out, OR, SUBU, ADD, ADDU, SLT, SUB, AND, XOR);
  and and_12 (R_TYPE, or_12_out, not_6_out);
  not not_6 (not_6_out, Halt);
  or or_13 (RegDst, OR, R_TYPE, AND, XOR, NOR);
  or or_14 (RegWrite, XOR, NOR, XOR, AND, MemToReg2, or_4_out, R_TYPE, ORI, LW, or_2_out, OR, ANDI, ORI, or_1_out);
  or or_15 (or_15_out, or_1_out, SLT);
  Priority_Encoder #(.select(4), .disabled("Z")) priority_encoder_1 (
    .in5(or_6_out), .in6(or_3_out), .in7(or_10_out), .in8(or_11_out), .in9(XOR), .in10(NOR),
    .in11(or_15_out), .out(ALU_OP), .en_in(in_3));  // open: in0, in1, in2, in3, in4, in12, in13, in14, in15, gs, en_out
  // Probe on ALU_OP

  // Other names for the same wires on the sheet: LUI = MemToReg2; SysCall = Halt; XORI = XOR
endmodule

module ALU (
  input  [31:0] X,
  input  [31:0] Y,
  input  [3:0] AluOP,
  output Equal,
  output [31:0] Result,
  output [31:0] Result_2
);

  wire [0:0] comparator_1_lt, comparator_2_lt;
  wire [31:0] AND_out, divider_1_out, divider_1_rem, fa32_1_s, multiplier_1_cout, multiplier_1_out, NOR_out,
       OR_out, shifter_1_out, shifter_2_out, shifter_3_out, subtractor_1_out, XOR_out;

  fa32 fa32_1 (.in_1(1'b0), .A(X), .B(Y), .S(fa32_1_s));  // open: C32
  assign AND_out = X & Y;  // AND_Gate AND, 32 bits wide
  assign OR_out = X | Y;  // OR_Gate OR, 32 bits wide
  Shifter #(.width(32), .shift("ll")) shifter_1 (.in(X), .\dist (Y[4:0]), .out(shifter_1_out));
  Shifter #(.width(32), .shift("ar")) shifter_2 (.in(X), .\dist (Y[4:0]), .out(shifter_2_out));
  Shifter #(.width(32), .shift("lr")) shifter_3 (.in(X), .\dist (Y[4:0]), .out(shifter_3_out));
  Multiplier #(.width(32)) multiplier_1 (.a(X), .b(Y), .out(multiplier_1_out), .cout(multiplier_1_cout));  // open: cin
  Divider #(.width(32)) divider_1 (.a(X), .b(Y), .out(divider_1_out), .rem(divider_1_rem));  // open: upper
  Subtractor #(.width(32)) subtractor_1 (.a(X), .b(Y), .out(subtractor_1_out));  // open: bin, bout
  assign XOR_out = X ^ Y;  // XOR_Gate XOR, 32 bits wide
  assign NOR_out = ~(X | Y);  // NOR_Gate NOR, 32 bits wide
  Comparator #(.width(32), .mode("twosComplement")) comparator_1 (
    .a(X), .b(Y), .eq(Equal), .lt(comparator_1_lt[0]));  // open: gt
  Comparator #(.width(32), .mode("unsigned")) comparator_2 (.a(X), .b(Y), .lt(comparator_2_lt[0]));  // open: gt, eq
  Multiplexer #(.select(4), .width(32), .disabled("Z"), .enable("false")) multiplexer_1 (
    .in0(shifter_1_out), .in1(shifter_2_out), .in2(shifter_3_out), .in3(multiplier_1_out),
    .in4(divider_1_out), .in5(fa32_1_s), .in6(subtractor_1_out), .in7(AND_out), .in8(OR_out), .in9(XOR_out),
    .in10(NOR_out), .in11({{31{1'b0}}, comparator_1_lt[0]}), .in12({{31{1'b0}}, comparator_2_lt[0]}),
    .in13({32{1'b0}}), .in14({32{1'b0}}), .in15({32{1'b0}}), .out(Result), .sel(AluOP));
  Multiplexer #(.select(4), .width(32), .disabled("Z"), .enable("false")) multiplexer_2 (
    .in0({32{1'b0}}), .in1({32{1'b0}}), .in2({32{1'b0}}), .in3(multiplier_1_cout), .in4(divider_1_rem),
    .in5({32{1'b0}}), .in6({32{1'b0}}), .in7({32{1'b0}}), .in8({32{1'b0}}), .in9({32{1'b0}}),
    .in10({32{1'b0}}), .in11({32{1'b0}}), .in12({32{1'b0}}), .in13({32{1'b0}}), .in14({32{1'b0}}),
    .in15({32{1'b0}}), .out(Result_2), .sel(AluOP));

  // Other names for the same wires on the sheet: Result2[31:0] = Result_2; S[3:0] = AluOP

  // Notes on the sheet:
  //   5
  //   6
  //   7
  //   8
  //   9
  //   10
  //   11
  //   输入引脚
  //   输出引脚
endmodule

module RF10 (
  input  in_1,
  input  WE3,
  input  [3:0] A3,
  input  [3:0] A1,
  input  [31:0] WD,
  input  [3:0] A2,
  output [31:0] RD1,
  output [31:0] RD2
);

  wire decoder_1_out0, decoder_1_out1, decoder_1_out2, decoder_1_out3, decoder_1_out4, decoder_1_out5,
       decoder_1_out6, decoder_1_out7, decoder_1_out8, decoder_1_out9;
  wire [31:0] register_1_q, register_2_q, register_3_q, register_4_q, register_5_q, register_6_q,
       register_7_q, register_8_q, register_9_q, register_10_q;

  Decoder #(.select(4), .tristate("false"), .disabled(0), .enable("true")) decoder_1 (
    .out0(decoder_1_out0), .out1(decoder_1_out1), .out2(decoder_1_out2), .out3(decoder_1_out3),
    .out4(decoder_1_out4), .out5(decoder_1_out5), .out6(decoder_1_out6), .out7(decoder_1_out7),
    .out8(decoder_1_out8), .out9(decoder_1_out9), .sel(A3), .en(WE3));  // open: out10, out11, out12, out13, out14, out15
  Register #(.width(32), .trigger("rising"), .Select("low")) register_1 (
    .D(WD), .en(decoder_1_out0), .Q(register_1_q), .clk(in_1));  // open: clr
  Register #(.width(32), .trigger("rising"), .Select("low")) register_2 (
    .D(WD), .en(decoder_1_out1), .Q(register_2_q), .clk(in_1));  // open: clr
  Register #(.width(32), .trigger("rising"), .Select("low")) register_3 (
    .D(WD), .en(decoder_1_out2), .Q(register_3_q), .clk(in_1));  // open: clr
  Register #(.width(32), .trigger("rising"), .Select("low")) register_4 (
    .D(WD), .en(decoder_1_out3), .Q(register_4_q), .clk(in_1));  // open: clr
  Register #(.width(32), .trigger("rising"), .Select("low")) register_5 (
    .D(WD), .en(decoder_1_out4), .Q(register_5_q), .clk(in_1));  // open: clr
  Register #(.width(32), .trigger("rising"), .Select("low")) register_6 (
    .D(WD), .en(decoder_1_out5), .Q(register_6_q), .clk(in_1));  // open: clr
  Register #(.width(32), .trigger("rising"), .Select("low")) register_7 (
    .D(WD), .en(decoder_1_out6), .Q(register_7_q), .clk(in_1));  // open: clr
  Register #(.width(32), .trigger("rising"), .Select("low")) register_8 (
    .D(WD), .en(decoder_1_out7), .Q(register_8_q), .clk(in_1));  // open: clr
  Register #(.width(32), .trigger("rising"), .Select("low")) register_9 (
    .D(WD), .en(decoder_1_out8), .Q(register_9_q), .clk(in_1));  // open: clr
  Register #(.width(32), .trigger("rising"), .Select("low")) register_10 (
    .D(WD), .en(decoder_1_out9), .Q(register_10_q), .clk(in_1));  // open: clr
  Multiplexer #(.select(4), .width(32), .disabled("Z"), .enable("false")) multiplexer_1 (
    .in0(register_1_q), .in1(register_2_q), .in2(register_3_q), .in3(register_4_q), .in4(register_5_q),
    .in5(register_6_q), .in6(register_7_q), .in7(register_8_q), .in8(register_9_q), .in9(register_10_q),
    .out(RD1), .sel(A1));  // open: in10, in11, in12, in13, in14, in15
  Multiplexer #(.select(4), .width(32), .disabled("Z"), .enable("false")) multiplexer_2 (
    .in0(register_1_q), .in1(register_2_q), .in2(register_3_q), .in3(register_4_q), .in4(register_5_q),
    .in5(register_6_q), .in6(register_7_q), .in7(register_8_q), .in8(register_9_q), .in9(register_10_q),
    .out(RD2), .sel(A2));  // open: in10, in11, in12, in13, in14, in15
endmodule

module hp (
  input  A,
  input  B,
  output S,
  output Cout
);

  and and_1 (Cout, B, A);
  xor xor_1 (S, B, A);
endmodule

module fa (
  input  in_1,
  input  in_2,
  input  in_3,
  output out_4,
  output out_5
);

  wire hp_1_cout, hp_1_s, hp_2_cout;

  hp hp_1 (.A(in_2), .B(in_3), .S(hp_1_s), .Cout(hp_1_cout));
  hp hp_2 (.A(in_1), .B(hp_1_s), .S(out_4), .Cout(hp_2_cout));
  or or_1 (out_5, hp_2_cout, hp_1_cout);
endmodule

module fa4 (
  input  C0,
  input  [3:0] A,
  input  [3:0] B,
  output [3:0] S,
  output C4
);

  wire fa_1_out_5, fa_2_out_5, fa_3_out_5;

  fa fa_1 (.in_1(C0), .in_2(A[0]), .in_3(B[0]), .out_4(S[0]), .out_5(fa_1_out_5));
  fa fa_2 (.in_1(fa_1_out_5), .in_2(A[1]), .in_3(B[1]), .out_4(S[1]), .out_5(fa_2_out_5));
  fa fa_3 (.in_1(fa_2_out_5), .in_2(A[2]), .in_3(B[2]), .out_4(S[2]), .out_5(fa_3_out_5));
  fa fa_4 (.in_1(fa_3_out_5), .in_2(A[3]), .in_3(B[3]), .out_4(S[3]), .out_5(C4));
endmodule

module fa16 (
  input  C0,
  input  [15:0] A,
  input  [15:0] B,
  output [15:0] S,
  output C16
);

  wire fa4_1_c4, fa4_2_c4, fa4_3_c4;

  fa4 fa4_1 (.C0(C0), .A(A[3:0]), .B(B[3:0]), .S(S[3:0]), .C4(fa4_1_c4));
  fa4 fa4_2 (.C0(fa4_1_c4), .A(A[7:4]), .B(B[7:4]), .S(S[7:4]), .C4(fa4_2_c4));
  fa4 fa4_3 (.C0(fa4_2_c4), .A(A[11:8]), .B(B[11:8]), .S(S[11:8]), .C4(fa4_3_c4));
  fa4 fa4_4 (.C0(fa4_3_c4), .A(A[15:12]), .B(B[15:12]), .S(S[15:12]), .C4(C16));
endmodule

module fa32 (
  input  in_1,
  input  [31:0] A,
  input  [31:0] B,
  output [31:0] S,
  output C32
);

  wire fa16_1_c16;

  fa16 fa16_1 (.C0(in_1), .A(A[15:0]), .B(B[15:0]), .S(S[15:0]), .C16(fa16_1_c16));
  fa16 fa16_2 (.C0(fa16_1_c16), .A(A[31:16]), .B(B[31:16]), .S(S[31:16]), .C16(C32));
endmodule

module RegiFile (
  input  [31:0] Din,
  input  Clk,
  input  WE,
  input  [4:0] R1_num,
  input  [4:0] W_num,
  input  [4:0] R2_num,
  output [31:0] R1,
  output [31:0] R2
);

  // RegisterFile registerfile_1: pin names not known; wires that end beside it: Din, Clk, WE, W_num, R1_num, R2_num, R1, R2
endmodule
