// Logisim project control.circ as structural Verilog: 5 circuits, main circuit Control
module Control (
  input  [5:0] op,
  input  [5:0] Funct,
  output IsJAL,
  output MemRead,
  output IsShamt,
  output MemWrite,
  output MemtoReg,
  output Jump,
  output RegWrite,
  output Branch,
  output BneOrBeq,
  output RegDst,
  output [3:0] ALUop,
  output ALUSrc,
  output IsJR,
  output IsSyscall,
  output IsCOP0,
  output ReadRs,
  output ZeroExtend,
  output ReadRt
);

  wire funct_decoder_1_isjr, funct_decoder_1_isshamt, funct_decoder_1_issyscall, IsSpecial, not_1_out;
  wire [3:0] alu_decoder_1_aluop3, funct_decoder_1_alu3;

  Opcode_Decoder opcode_decoder_1 (
    .op0(op[5]), .MemRead(MemRead), .op1(op[4]), .op2(op[3]), .MemWrite(MemWrite), .op3(op[2]), .op4(op[1]),
    .op5(op[0]), .ALUSrc(ALUSrc), .Jump(Jump), .MemtoReg(MemtoReg), .Branch(Branch), .RegDst(RegDst),
    .RegWrite(RegWrite), .BneBeq(BneOrBeq), .IsJAL(IsJAL), .ZeroExtend(ZeroExtend));
  RegisterRead_Detector registerread_detector_1 (
    .op0(op[5]), .op1(op[4]), .op2(op[3]), .op3(op[2]), .op4(op[1]), .op5(op[0]), .Funct0(Funct[5]),
    .Funct1(Funct[4]), .Funct2(Funct[3]), .Funct3(Funct[2]), .Funct4(Funct[1]), .Funct5(Funct[0]),
    .ReadRs(ReadRs), .ReadRt(ReadRt));
  Funct_Decoder funct_decoder_1 (
    .Funct0(Funct[5]), .Funct1(Funct[4]), .Funct2(Funct[3]), .Funct3(Funct[2]),
    .ALU0(funct_decoder_1_alu3[3]), .Funct4(Funct[1]), .Funct5(Funct[0]), .ALU1(funct_decoder_1_alu3[2]),
    .ALU2(funct_decoder_1_alu3[1]), .ALU3(funct_decoder_1_alu3[0]), .IsJR(funct_decoder_1_isjr),
    .IsSyscall(funct_decoder_1_issyscall), .IsShamt(funct_decoder_1_isshamt));
  ALU_Decoder alu_decoder_1 (
    .op0(op[5]), .op1(op[4]), .op2(op[3]), .ALUop0(alu_decoder_1_aluop3[3]), .op3(op[2]), .op4(op[1]),
    .op5(op[0]), .ALUop1(alu_decoder_1_aluop3[2]), .ALUop2(alu_decoder_1_aluop3[1]),
    .ALUop3(alu_decoder_1_aluop3[0]));
  and and_1 (IsCOP0, ~op[5], op[4], ~op[3], ~op[2], ~op[1], ~op[0]);  // AND_Gate
  Multiplexer #(.select(1), .width(1), .disabled("Z"), .enable("false")) multiplexer_1 (
    .in0(1'b0), .in1(funct_decoder_1_issyscall), .out(IsSyscall), .sel(IsSpecial));
  Multiplexer #(.select(1), .width(1), .disabled("Z"), .enable("false")) multiplexer_2 (
    .in0(1'b0), .in1(funct_decoder_1_isjr), .out(IsJR), .sel(IsSpecial));
  Multiplexer #(.select(1), .width(1), .disabled("Z"), .enable("false")) multiplexer_3 (
    .in0(1'b0), .in1(funct_decoder_1_isshamt), .out(IsShamt), .sel(IsSpecial));
  not not_1 (not_1_out, IsSpecial);
  Multiplexer #(.select(1), .width(4), .disabled("Z"), .enable("false")) multiplexer_4 (
    .in0(funct_decoder_1_alu3), .in1(alu_decoder_1_aluop3), .out(ALUop), .sel(not_1_out));
  and and_2 (IsSpecial, ~op[5], ~op[4], ~op[3], ~op[2], ~op[1], ~op[0]);  // AND_Gate

  // Notes on the sheet:
  //   Input & Output
  //   OP Decoding
  //   ALU Decoding
endmodule

module Funct_Decoder (
  input  Funct0,
  input  Funct1,
  input  Funct2,
  input  Funct3,
  input  Funct4,
  input  Funct5,
  output ALU0,
  output ALU1,
  output ALU2,
  output ALU3,
  output IsJR,
  output IsSyscall,
  output IsShamt
);

  wire and_1_out, and_2_out, and_3_out, and_4_out, and_5_out, and_6_out, and_7_out, and_8_out, and_9_out,
       and_10_out, and_11_out, and_12_out, and_13_out, and_14_out, and_15_out, and_16_out, and_17_out,
       and_20_out, and_21_out, and_22_out, not_1_out, not_2_out, not_3_out, not_4_out, not_5_out, not_6_out,
       not_7_out, not_8_out, not_9_out, not_10_out, not_11_out, not_12_out, not_13_out, not_14_out,
       not_15_out, not_16_out, not_17_out, not_18_out, not_19_out, not_20_out, not_21_out, not_22_out,
       not_23_out, not_24_out, not_25_out, not_26_out, not_27_out, not_28_out, not_29_out, not_30_out,
       not_31_out, not_32_out, not_33_out, not_34_out, not_35_out, not_36_out, not_37_out, not_38_out,
       not_39_out, not_40_out, not_41_out, not_42_out, not_43_out, not_44_out, not_45_out, not_46_out,
       not_47_out, not_48_out, not_49_out, not_50_out, not_51_out, not_52_out, not_53_out, not_54_out,
       not_55_out, not_56_out, not_57_out, not_58_out, not_59_out, not_60_out, not_61_out, not_62_out,
       not_63_out, not_64_out, not_65_out, not_66_out, not_67_out, not_68_out, not_69_out, not_70_out,
       not_71_out, not_72_out, not_73_out, not_74_out, not_75_out, not_76_out, not_77_out, not_78_out,
       not_79_out, not_80_out, not_81_out;

  not not_1 (not_1_out, Funct1);
  not not_2 (not_2_out, Funct2);
  not not_3 (not_3_out, Funct4);
  not not_4 (not_4_out, Funct1);
  not not_5 (not_5_out, Funct2);
  not not_6 (not_6_out, Funct1);
  not not_7 (not_7_out, Funct3);
  not not_8 (not_8_out, Funct5);
  not not_9 (not_9_out, Funct1);
  not not_10 (not_10_out, Funct3);
  not not_11 (not_11_out, Funct1);
  not not_12 (not_12_out, Funct2);
  not not_13 (not_13_out, Funct3);
  not not_14 (not_14_out, Funct4);
  not not_15 (not_15_out, Funct1);
  not not_16 (not_16_out, Funct2);
  not not_17 (not_17_out, Funct3);
  not not_18 (not_18_out, Funct5);
  not not_19 (not_19_out, Funct1);
  not not_20 (not_20_out, Funct2);
  not not_21 (not_21_out, Funct4);
  not not_22 (not_22_out, Funct5);
  not not_23 (not_23_out, Funct1);
  not not_24 (not_24_out, Funct3);
  not not_25 (not_25_out, Funct1);
  not not_26 (not_26_out, Funct2);
  not not_27 (not_27_out, Funct3);
  not not_28 (not_28_out, Funct5);
  not not_29 (not_29_out, Funct1);
  not not_30 (not_30_out, Funct2);
  not not_31 (not_31_out, Funct4);
  not not_32 (not_32_out, Funct5);
  not not_33 (not_33_out, Funct0);
  not not_34 (not_34_out, Funct1);
  not not_35 (not_35_out, Funct2);
  not not_36 (not_36_out, Funct3);
  not not_37 (not_37_out, Funct5);
  not not_38 (not_38_out, Funct1);
  not not_39 (not_39_out, Funct2);
  not not_40 (not_40_out, Funct1);
  not not_41 (not_41_out, Funct3);
  not not_42 (not_42_out, Funct5);
  not not_43 (not_43_out, Funct0);
  not not_44 (not_44_out, Funct1);
  not not_45 (not_45_out, Funct2);
  not not_46 (not_46_out, Funct3);
  not not_47 (not_47_out, Funct1);
  not not_48 (not_48_out, Funct2);
  not not_49 (not_49_out, Funct3);
  not not_50 (not_50_out, Funct4);
  not not_51 (not_51_out, Funct1);
  not not_52 (not_52_out, Funct2);
  not not_53 (not_53_out, Funct4);
  not not_54 (not_54_out, Funct5);
  not not_55 (not_55_out, Funct1);
  not not_56 (not_56_out, Funct3);
  not not_57 (not_57_out, Funct5);
  not not_58 (not_58_out, Funct0);
  not not_59 (not_59_out, Funct1);
  not not_60 (not_60_out, Funct3);
  not not_61 (not_61_out, Funct4);
  not not_62 (not_62_out, Funct5);
  not not_63 (not_63_out, Funct0);
  not not_64 (not_64_out, Funct1);
  not not_65 (not_65_out, Funct4);
  not not_66 (not_66_out, Funct5);
  not not_67 (not_67_out, Funct0);
  not not_68 (not_68_out, Funct1);
  not not_69 (not_69_out, Funct2);
  not not_70 (not_70_out, Funct3);
  not not_71 (not_71_out, Funct0);
  not not_72 (not_72_out, Funct1);
  not not_73 (not_73_out, Funct2);
  not not_74 (not_74_out, Funct3);
  not not_75 (not_75_out, Funct5);
  not not_76 (not_76_out, Funct0);
  not not_77 (not_77_out, Funct1);
  not not_78 (not_78_out, Funct2);
  not not_79 (not_79_out, Funct3);
  not not_80 (not_80_out, Funct4);
  not not_81 (not_81_out, Funct5);
  and and_1 (and_1_out, Funct0, not_1_out, not_2_out, Funct3, not_3_out, Funct5);
  and and_2 (and_2_out, Funct0, not_4_out, not_5_out, Funct3, Funct4, Funct5);
  and and_3 (and_3_out, Funct0, not_6_out, Funct2, not_7_out, Funct4, not_8_out);
  and and_4 (and_4_out, Funct0, not_9_out, Funct2, not_10_out, Funct4, Funct5);
  and and_5 (and_5_out, Funct0, not_11_out, not_12_out, not_13_out, not_14_out);
  and and_6 (and_6_out, Funct0, not_15_out, not_16_out, not_17_out, not_18_out);
  and and_7 (and_7_out, Funct0, not_19_out, not_20_out, not_21_out, not_22_out);
  and and_8 (and_8_out, Funct0, not_23_out, Funct2, not_24_out, Funct4, Funct5);
  and and_9 (and_9_out, Funct0, not_25_out, not_26_out, not_27_out, Funct4, not_28_out);
  and and_10 (and_10_out, Funct0, not_29_out, not_30_out, Funct3, not_31_out, not_32_out);
  and and_11 (and_11_out, not_33_out, not_34_out, not_35_out, not_36_out, Funct4, not_37_out);
  and and_12 (and_12_out, Funct0, not_38_out, not_39_out, Funct3, Funct4, Funct5);
  and and_13 (and_13_out, Funct0, not_40_out, Funct2, not_41_out, Funct4, not_42_out);
  and and_14 (and_14_out, not_43_out, not_44_out, not_45_out, not_46_out, Funct4, Funct5);
  and and_15 (and_15_out, Funct0, not_47_out, not_48_out, not_49_out, not_50_out);
  and and_16 (and_16_out, Funct0, not_51_out, not_52_out, not_53_out, not_54_out);
  and and_17 (and_17_out, Funct0, not_55_out, Funct2, not_56_out, Funct4, not_57_out);
  and and_18 (IsJR, not_58_out, not_59_out, Funct2, not_60_out, not_61_out, not_62_out);
  and and_19 (IsSyscall, not_63_out, not_64_out, Funct2, Funct3, not_65_out, not_66_out);
  and and_20 (and_20_out, not_67_out, not_68_out, not_69_out, not_70_out, Funct4, Funct5);
  and and_21 (and_21_out, not_71_out, not_72_out, not_73_out, not_74_out, Funct4, not_75_out);
  and and_22 (and_22_out, not_76_out, not_77_out, not_78_out, not_79_out, not_80_out, not_81_out);
  or or_1 (ALU0, and_1_out, and_2_out, and_3_out, and_4_out);
  or or_2 (ALU1, and_5_out, and_6_out, and_7_out, and_8_out);
  or or_3 (ALU2, and_9_out, and_10_out, and_11_out, and_12_out, and_13_out);
  or or_4 (ALU3, and_14_out, and_15_out, and_16_out, and_17_out);
  or or_5 (IsShamt, and_20_out, and_21_out, and_22_out);
endmodule

module ALU_Decoder (
  input  op0,
  input  op1,
  input  op2,
  input  op3,
  input  op4,
  input  op5,
  output ALUop0,
  output ALUop1,
  output ALUop2,
  output ALUop3
);

  wire and_1_out, and_2_out, and_3_out, and_4_out, and_5_out, and_6_out, and_7_out, and_8_out, and_9_out,
       and_10_out, and_11_out, and_12_out, and_13_out, and_14_out, and_15_out, and_16_out, and_17_out,
       and_18_out, and_19_out, and_20_out, and_21_out, and_22_out, and_23_out, and_24_out, and_25_out,
       and_26_out, and_27_out, and_28_out, and_29_out, not_1_out, not_2_out, not_3_out, not_4_out, not_5_out,
       not_6_out, not_7_out, not_8_out, not_9_out, not_10_out, not_11_out, not_12_out, not_13_out,
       not_14_out, not_15_out, not_16_out, not_17_out, not_18_out, not_19_out, not_20_out, not_21_out,
       not_22_out, not_23_out, not_24_out, not_25_out, not_26_out, not_27_out, not_28_out, not_29_out,
       not_30_out, not_31_out, not_32_out, not_33_out, not_34_out, not_35_out, not_36_out, not_37_out,
       not_38_out, not_39_out, not_40_out, not_41_out, not_42_out, not_43_out, not_44_out, not_45_out,
       not_46_out, not_47_out, not_48_out, not_49_out, not_50_out, not_51_out, not_52_out, not_53_out,
       not_54_out, not_55_out, not_56_out, not_57_out, not_58_out, not_59_out, not_60_out, not_61_out,
       not_62_out, not_63_out, not_64_out, not_65_out, not_66_out, not_67_out, not_68_out, not_69_out,
       not_70_out, not_71_out, not_72_out, not_73_out, not_74_out, not_75_out, not_76_out, not_77_out,
       not_78_out, not_79_out, not_80_out, not_81_out, not_82_out, not_83_out, not_84_out, not_85_out,
       not_86_out, not_87_out, not_88_out, not_89_out, not_90_out, not_91_out, not_92_out, not_93_out,
       not_94_out, not_95_out, not_96_out, not_97_out, not_98_out, not_99_out, not_100_out, not_101_out,
       not_102_out, not_103_out, not_104_out, not_105_out, not_106_out, not_107_out, not_108_out,
       not_109_out, not_110_out, not_111_out, not_112_out, not_113_out, not_114_out, not_115_out,
       not_116_out, not_117_out, not_118_out, not_119_out, not_120_out, not_121_out, not_122_out, not_123_out;

  not not_1 (not_1_out, op0);
  not not_2 (not_2_out, op1);
  not not_3 (not_3_out, op4);
  not not_4 (not_4_out, op0);
  not not_5 (not_5_out, op1);
  not not_6 (not_6_out, op3);
  not not_7 (not_7_out, op5);
  not not_8 (not_8_out, op0);
  not not_9 (not_9_out, op1);
  not not_10 (not_10_out, op2);
  not not_11 (not_11_out, op3);
  not not_12 (not_12_out, op4);
  not not_13 (not_13_out, op5);
  not not_14 (not_14_out, op0);
  not not_15 (not_15_out, op1);
  not not_16 (not_16_out, op3);
  not not_17 (not_17_out, op4);
  not not_18 (not_18_out, op5);
  not not_19 (not_19_out, op1);
  not not_20 (not_20_out, op2);
  not not_21 (not_21_out, op3);
  not not_22 (not_22_out, op1);
  not not_23 (not_23_out, op3);
  not not_24 (not_24_out, op0);
  not not_25 (not_25_out, op1);
  not not_26 (not_26_out, op2);
  not not_27 (not_27_out, op4);
  not not_28 (not_28_out, op0);
  not not_29 (not_29_out, op1);
  not not_30 (not_30_out, op2);
  not not_31 (not_31_out, op4);
  not not_32 (not_32_out, op5);
  not not_33 (not_33_out, op0);
  not not_34 (not_34_out, op1);
  not not_35 (not_35_out, op4);
  not not_36 (not_36_out, op5);
  not not_37 (not_37_out, op0);
  not not_38 (not_38_out, op1);
  not not_39 (not_39_out, op3);
  not not_40 (not_40_out, op4);
  not not_41 (not_41_out, op0);
  not not_42 (not_42_out, op1);
  not not_43 (not_43_out, op3);
  not not_44 (not_44_out, op4);
  not not_45 (not_45_out, op5);
  not not_46 (not_46_out, op0);
  not not_47 (not_47_out, op1);
  not not_48 (not_48_out, op2);
  not not_49 (not_49_out, op3);
  not not_50 (not_50_out, op5);
  not not_51 (not_51_out, op0);
  not not_52 (not_52_out, op1);
  not not_53 (not_53_out, op2);
  not not_54 (not_54_out, op3);
  not not_55 (not_55_out, op0);
  not not_56 (not_56_out, op2);
  not not_57 (not_57_out, op3);
  not not_58 (not_58_out, op4);
  not not_59 (not_59_out, op5);
  not not_60 (not_60_out, op0);
  not not_61 (not_61_out, op1);
  not not_62 (not_62_out, op4);
  not not_63 (not_63_out, op5);
  not not_64 (not_64_out, op0);
  not not_65 (not_65_out, op1);
  not not_66 (not_66_out, op3);
  not not_67 (not_67_out, op5);
  not not_68 (not_68_out, op0);
  not not_69 (not_69_out, op1);
  not not_70 (not_70_out, op2);
  not not_71 (not_71_out, op3);
  not not_72 (not_72_out, op4);
  not not_73 (not_73_out, op5);
  not not_74 (not_74_out, op0);
  not not_75 (not_75_out, op1);
  not not_76 (not_76_out, op3);
  not not_77 (not_77_out, op4);
  not not_78 (not_78_out, op5);
  not not_79 (not_79_out, op1);
  not not_80 (not_80_out, op2);
  not not_81 (not_81_out, op3);
  not not_82 (not_82_out, op1);
  not not_83 (not_83_out, op3);
  not not_84 (not_84_out, op0);
  not not_85 (not_85_out, op1);
  not not_86 (not_86_out, op2);
  not not_87 (not_87_out, op4);
  not not_88 (not_88_out, op0);
  not not_89 (not_89_out, op1);
  not not_90 (not_90_out, op2);
  not not_91 (not_91_out, op4);
  not not_92 (not_92_out, op5);
  not not_93 (not_93_out, op0);
  not not_94 (not_94_out, op1);
  not not_95 (not_95_out, op4);
  not not_96 (not_96_out, op5);
  not not_97 (not_97_out, op0);
  not not_98 (not_98_out, op1);
  not not_99 (not_99_out, op3);
  not not_100 (not_100_out, op5);
  not not_101 (not_101_out, op0);
  not not_102 (not_102_out, op1);
  not not_103 (not_103_out, op3);
  not not_104 (not_104_out, op4);
  not not_105 (not_105_out, op0);
  not not_106 (not_106_out, op1);
  not not_107 (not_107_out, op3);
  not not_108 (not_108_out, op4);
  not not_109 (not_109_out, op5);
  not not_110 (not_110_out, op0);
  not not_111 (not_111_out, op1);
  not not_112 (not_112_out, op2);
  not not_113 (not_113_out, op3);
  not not_114 (not_114_out, op5);
  not not_115 (not_115_out, op0);
  not not_116 (not_116_out, op1);
  not not_117 (not_117_out, op2);
  not not_118 (not_118_out, op3);
  not not_119 (not_119_out, op0);
  not not_120 (not_120_out, op2);
  not not_121 (not_121_out, op3);
  not not_122 (not_122_out, op4);
  not not_123 (not_123_out, op5);
  and and_1 (and_1_out, not_1_out, not_2_out, op2, op3, not_3_out, op5);
  and and_2 (and_2_out, not_4_out, not_5_out, op2, not_6_out, op4, not_7_out);
  and and_3 (and_3_out, not_8_out, not_9_out, not_10_out, not_11_out, not_12_out, not_13_out);
  and and_4 (and_4_out, not_14_out, not_15_out, op2, not_16_out, not_17_out, not_18_out);
  and and_5 (and_5_out, op0, not_19_out, not_20_out, not_21_out, op4, op5);
  and and_6 (and_6_out, op0, not_22_out, op2, not_23_out, op4, op5);
  and and_7 (and_7_out, not_24_out, not_25_out, not_26_out, op3, not_27_out, op5);
  and and_8 (and_8_out, not_28_out, not_29_out, not_30_out, op3, not_31_out, not_32_out);
  and and_9 (and_9_out, not_33_out, not_34_out, op2, op3, not_35_out, not_36_out);
  and and_10 (and_10_out, not_37_out, not_38_out, op2, not_39_out, not_40_out, op5);
  and and_11 (and_11_out, not_41_out, not_42_out, op2, not_43_out, not_44_out, not_45_out);
  and and_12 (and_12_out, not_46_out, not_47_out, not_48_out, not_49_out, op4, not_50_out);
  and and_13 (and_13_out, not_51_out, not_52_out, not_53_out, not_54_out, op4, op5);
  and and_14 (and_14_out, not_55_out, op1, not_56_out, not_57_out, not_58_out, not_59_out);
  and and_15 (and_15_out, not_60_out, not_61_out, op2, op3, not_62_out, not_63_out);
  and and_16 (and_16_out, not_64_out, not_65_out, op2, not_66_out, op4, not_67_out);
  and and_17 (and_17_out, not_68_out, not_69_out, not_70_out, not_71_out, not_72_out, not_73_out);
  and and_18 (and_18_out, not_74_out, not_75_out, op2, not_76_out, not_77_out, not_78_out);
  and and_19 (and_19_out, op0, not_79_out, not_80_out, not_81_out, op4, op5);
  and and_20 (and_20_out, op0, not_82_out, op2, not_83_out, op4, op5);
  and and_21 (and_21_out, not_84_out, not_85_out, not_86_out, op3, not_87_out, op5);
  and and_22 (and_22_out, not_88_out, not_89_out, not_90_out, op3, not_91_out, not_92_out);
  and and_23 (and_23_out, not_93_out, not_94_out, op2, op3, not_95_out, not_96_out);
  and and_24 (and_24_out, not_97_out, not_98_out, op2, not_99_out, op4, not_100_out);
  and and_25 (and_25_out, not_101_out, not_102_out, op2, not_103_out, not_104_out, op5);
  and and_26 (and_26_out, not_105_out, not_106_out, op2, not_107_out, not_108_out, not_109_out);
  and and_27 (and_27_out, not_110_out, not_111_out, not_112_out, not_113_out, op4, not_114_out);
  and and_28 (and_28_out, not_115_out, not_116_out, not_117_out, not_118_out, op4, op5);
  and and_29 (and_29_out, not_119_out, op1, not_120_out, not_121_out, not_122_out, not_123_out);
  or or_1 (ALUop0, and_1_out, and_2_out);
  or or_2 (ALUop2, and_15_out, and_16_out);
  or or_3 (ALUop1, and_3_out, and_4_out, and_5_out, and_6_out, and_7_out, and_8_out, and_9_out, and_10_out, and_11_out, and_12_out, and_13_out, and_14_out);
  or or_4 (ALUop3, and_17_out, and_18_out, and_19_out, and_20_out, and_21_out, and_22_out, and_23_out, and_24_out, and_25_out, and_26_out, and_27_out, and_28_out, and_29_out);
endmodule

module Opcode_Decoder (
  input  op0,
  input  op1,
  input  op2,
  input  op3,
  input  op4,
  input  op5,
  output MemRead,
  output MemWrite,
  output ALUSrc,
  output Jump,
  output MemtoReg,
  output Branch,
  output RegDst,
  output RegWrite,
  output BneBeq,
  output IsJAL,
  output ZeroExtend
);

  wire and_3_out, and_4_out, and_5_out, and_6_out, and_7_out, and_8_out, and_9_out, and_10_out, and_11_out,
       and_12_out, and_14_out, and_15_out, and_17_out, and_18_out, and_19_out, and_20_out, and_21_out,
       and_22_out, and_23_out, and_24_out, and_25_out, and_26_out, and_29_out, and_30_out, not_1_out,
       not_2_out, not_3_out, not_4_out, not_5_out, not_6_out, not_7_out, not_8_out, not_9_out, not_10_out,
       not_11_out, not_12_out, not_13_out, not_14_out, not_15_out, not_16_out, not_17_out, not_18_out,
       not_19_out, not_20_out, not_21_out, not_22_out, not_23_out, not_24_out, not_25_out, not_26_out,
       not_27_out, not_28_out, not_29_out, not_30_out, not_31_out, not_32_out, not_33_out, not_34_out,
       not_35_out, not_36_out, not_37_out, not_38_out, not_39_out, not_40_out, not_41_out, not_42_out,
       not_43_out, not_44_out, not_45_out, not_46_out, not_47_out, not_48_out, not_49_out, not_50_out,
       not_51_out, not_52_out, not_53_out, not_54_out, not_55_out, not_56_out, not_57_out, not_58_out,
       not_59_out, not_60_out, not_61_out, not_62_out, not_63_out, not_64_out, not_65_out, not_66_out,
       not_67_out, not_68_out, not_69_out, not_70_out, not_71_out, not_72_out, not_73_out, not_74_out,
       not_75_out, not_76_out, not_77_out, not_78_out, not_79_out, not_80_out, not_81_out, not_82_out,
       not_83_out, not_84_out, not_85_out, not_86_out, not_87_out, not_88_out, not_89_out, not_90_out,
       not_91_out, not_92_out, not_93_out, not_94_out, not_95_out, not_96_out, not_97_out, not_98_out,
       not_99_out, not_100_out, not_101_out, not_102_out, not_103_out, not_104_out, not_105_out, not_106_out,
       not_107_out, not_108_out, not_109_out, not_110_out, not_111_out, not_112_out, not_113_out,
       not_114_out, not_115_out, not_116_out, not_117_out, not_118_out, not_119_out;

  not not_1 (not_1_out, op1);
  not not_2 (not_2_out, op2);
  not not_3 (not_3_out, op3);
  not not_4 (not_4_out, op1);
  not not_5 (not_5_out, op3);
  not not_6 (not_6_out, op0);
  not not_7 (not_7_out, op1);
  not not_8 (not_8_out, op3);
  not not_9 (not_9_out, op4);
  not not_10 (not_10_out, op5);
  not not_11 (not_11_out, op1);
  not not_12 (not_12_out, op2);
  not not_13 (not_13_out, op3);
  not not_14 (not_14_out, op1);
  not not_15 (not_15_out, op3);
  not not_16 (not_16_out, op0);
  not not_17 (not_17_out, op1);
  not not_18 (not_18_out, op4);
  not not_19 (not_19_out, op5);
  not not_20 (not_20_out, op0);
  not not_21 (not_21_out, op1);
  not not_22 (not_22_out, op4);
  not not_23 (not_23_out, op0);
  not not_24 (not_24_out, op1);
  not not_25 (not_25_out, op3);
  not not_26 (not_26_out, op5);
  not not_27 (not_27_out, op0);
  not not_28 (not_28_out, op1);
  not not_29 (not_29_out, op3);
  not not_30 (not_30_out, op4);
  not not_31 (not_31_out, op0);
  not not_32 (not_32_out, op1);
  not not_33 (not_33_out, op3);
  not not_34 (not_34_out, op4);
  not not_35 (not_35_out, op5);
  not not_36 (not_36_out, op0);
  not not_37 (not_37_out, op1);
  not not_38 (not_38_out, op2);
  not not_39 (not_39_out, op3);
  not not_40 (not_40_out, op5);
  not not_41 (not_41_out, op0);
  not not_42 (not_42_out, op1);
  not not_43 (not_43_out, op2);
  not not_44 (not_44_out, op3);
  not not_45 (not_45_out, op1);
  not not_46 (not_46_out, op2);
  not not_47 (not_47_out, op3);
  not not_48 (not_48_out, op0);
  not not_49 (not_49_out, op1);
  not not_50 (not_50_out, op2);
  not not_51 (not_51_out, op4);
  not not_52 (not_52_out, op0);
  not not_53 (not_53_out, op1);
  not not_54 (not_54_out, op2);
  not not_55 (not_55_out, op4);
  not not_56 (not_56_out, op5);
  not not_57 (not_57_out, op0);
  not not_58 (not_58_out, op1);
  not not_59 (not_59_out, op2);
  not not_60 (not_60_out, op3);
  not not_61 (not_61_out, op4);
  not not_62 (not_62_out, op5);
  not not_63 (not_63_out, op0);
  not not_64 (not_64_out, op1);
  not not_65 (not_65_out, op2);
  not not_66 (not_66_out, op3);
  not not_67 (not_67_out, op4);
  not not_68 (not_68_out, op5);
  not not_69 (not_69_out, op0);
  not not_70 (not_70_out, op1);
  not not_71 (not_71_out, op3);
  not not_72 (not_72_out, op4);
  not not_73 (not_73_out, op5);
  not not_74 (not_74_out, op1);
  not not_75 (not_75_out, op2);
  not not_76 (not_76_out, op3);
  not not_77 (not_77_out, op0);
  not not_78 (not_78_out, op1);
  not not_79 (not_79_out, op4);
  not not_80 (not_80_out, op5);
  not not_81 (not_81_out, op0);
  not not_82 (not_82_out, op1);
  not not_83 (not_83_out, op4);
  not not_84 (not_84_out, op0);
  not not_85 (not_85_out, op1);
  not not_86 (not_86_out, op3);
  not not_87 (not_87_out, op5);
  not not_88 (not_88_out, op0);
  not not_89 (not_89_out, op1);
  not not_90 (not_90_out, op3);
  not not_91 (not_91_out, op4);
  not not_92 (not_92_out, op0);
  not not_93 (not_93_out, op1);
  not not_94 (not_94_out, op3);
  not not_95 (not_95_out, op4);
  not not_96 (not_96_out, op5);
  not not_97 (not_97_out, op0);
  not not_98 (not_98_out, op1);
  not not_99 (not_99_out, op2);
  not not_100 (not_100_out, op3);
  not not_101 (not_101_out, op0);
  not not_102 (not_102_out, op2);
  not not_103 (not_103_out, op3);
  not not_104 (not_104_out, op4);
  not not_105 (not_105_out, op5);
  not not_106 (not_106_out, op0);
  not not_107 (not_107_out, op1);
  not not_108 (not_108_out, op2);
  not not_109 (not_109_out, op4);
  not not_110 (not_110_out, op0);
  not not_111 (not_111_out, op1);
  not not_112 (not_112_out, op2);
  not not_113 (not_113_out, op3);
  not not_114 (not_114_out, op0);
  not not_115 (not_115_out, op1);
  not not_116 (not_116_out, op4);
  not not_117 (not_117_out, op0);
  not not_118 (not_118_out, op1);
  not not_119 (not_119_out, op5);
  and and_1 (MemRead, op0, not_1_out, not_2_out, not_3_out, op4, op5);
  and and_2 (MemWrite, op0, not_4_out, op2, not_5_out, op4, op5);
  and and_3 (and_3_out, not_6_out, not_7_out, op2, not_8_out, not_9_out, not_10_out);
  and and_4 (and_4_out, op0, not_11_out, not_12_out, not_13_out, op4, op5);
  and and_5 (and_5_out, op0, not_14_out, op2, not_15_out, op4, op5);
  and and_6 (and_6_out, not_16_out, not_17_out, op2, op3, not_18_out, not_19_out);
  and and_7 (and_7_out, not_20_out, not_21_out, op2, op3, not_22_out, op5);
  and and_8 (and_8_out, not_23_out, not_24_out, op2, not_25_out, op4, not_26_out);
  and and_9 (and_9_out, not_27_out, not_28_out, op2, not_29_out, not_30_out, op5);
  and and_10 (and_10_out, not_31_out, not_32_out, op2, not_33_out, not_34_out, not_35_out);
  and and_11 (and_11_out, not_36_out, not_37_out, not_38_out, not_39_out, op4, not_40_out);
  and and_12 (and_12_out, not_41_out, not_42_out, not_43_out, not_44_out, op4, op5);
  and and_13 (MemtoReg, op0, not_45_out, not_46_out, not_47_out, op4, op5);
  and and_14 (and_14_out, not_48_out, not_49_out, not_50_out, op3, not_51_out, op5);
  and and_15 (and_15_out, not_52_out, not_53_out, not_54_out, op3, not_55_out, not_56_out);
  and and_16 (RegDst, not_57_out, not_58_out, not_59_out, not_60_out, not_61_out, not_62_out);
  and and_17 (and_17_out, not_63_out, not_64_out, not_65_out, not_66_out, not_67_out, not_68_out);
  and and_18 (and_18_out, not_69_out, not_70_out, op2, not_71_out, not_72_out, not_73_out);
  and and_19 (and_19_out, op0, not_74_out, not_75_out, not_76_out, op4, op5);
  and and_20 (and_20_out, not_77_out, not_78_out, op2, op3, not_79_out, not_80_out);
  and and_21 (and_21_out, not_81_out, not_82_out, op2, op3, not_83_out, op5);
  and and_22 (and_22_out, not_84_out, not_85_out, op2, not_86_out, op4, not_87_out);
  and and_23 (and_23_out, not_88_out, not_89_out, op2, not_90_out, not_91_out, op5);
  and and_24 (and_24_out, not_92_out, not_93_out, op2, not_94_out, not_95_out, not_96_out);
  and and_25 (and_25_out, not_97_out, not_98_out, not_99_out, not_100_out, op4, op5);
  and and_26 (and_26_out, not_101_out, op1, not_102_out, not_103_out, not_104_out, not_105_out);
  and and_27 (BneBeq, not_106_out, not_107_out, not_108_out, op3, not_109_out, op5);
  and and_28 (IsJAL, not_110_out, not_111_out, not_112_out, not_113_out, op4, op5);
  and and_29 (and_29_out, not_114_out, not_115_out, op2, op3, not_116_out);
  and and_30 (and_30_out, not_117_out, not_118_out, op2, op3, op4, not_119_out);
  or or_1 (ALUSrc, and_3_out, and_4_out, and_5_out, and_6_out, and_7_out, and_8_out, and_9_out, and_10_out);
  or or_2 (Jump, and_11_out, and_12_out);
  or or_3 (Branch, and_14_out, and_15_out);
  or or_4 (ZeroExtend, and_29_out, and_30_out);
  or or_5 (RegWrite, and_17_out, and_18_out, and_19_out, and_20_out, and_21_out, and_22_out, and_23_out, and_24_out, and_25_out, and_26_out);
endmodule

module RegisterRead_Detector (
  input  op0,
  input  op1,
  input  op2,
  input  op3,
  input  op4,
  input  op5,
  input  Funct0,
  input  Funct1,
  input  Funct2,
  input  Funct3,
  input  Funct4,
  input  Funct5,
  output ReadRs,
  output ReadRt
);

  wire and_1_out, and_2_out, and_3_out, and_4_out, and_5_out, and_6_out, and_7_out, and_8_out, and_9_out,
       and_10_out, and_11_out, and_12_out, and_13_out, and_14_out, and_15_out, and_16_out, and_17_out,
       and_18_out, and_19_out, and_20_out, and_21_out, and_22_out, and_23_out, and_24_out, and_25_out,
       and_26_out, and_27_out, and_28_out, and_29_out, and_30_out, and_31_out, and_32_out, and_33_out,
       and_34_out, and_35_out, not_1_out, not_2_out, not_3_out, not_4_out, not_5_out, not_6_out, not_7_out,
       not_8_out, not_9_out, not_10_out, not_11_out, not_12_out, not_13_out, not_14_out, not_15_out,
       not_16_out, not_17_out, not_18_out, not_19_out, not_20_out, not_21_out, not_22_out, not_23_out,
       not_24_out, not_25_out, not_26_out, not_27_out, not_28_out, not_29_out, not_30_out, not_31_out,
       not_32_out, not_33_out, not_34_out, not_35_out, not_36_out, not_37_out, not_38_out, not_39_out,
       not_40_out, not_41_out, not_42_out, not_43_out, not_44_out, not_45_out, not_46_out, not_47_out,
       not_48_out, not_49_out, not_50_out, not_51_out, not_52_out, not_53_out, not_54_out, not_55_out,
       not_56_out, not_57_out, not_58_out, not_59_out, not_60_out, not_61_out, not_62_out, not_63_out,
       not_64_out, not_65_out, not_66_out, not_67_out, not_68_out, not_69_out, not_70_out, not_71_out,
       not_72_out, not_73_out, not_74_out, not_75_out, not_76_out, not_77_out, not_78_out, not_79_out,
       not_80_out, not_81_out, not_82_out, not_83_out, not_84_out, not_85_out, not_86_out, not_87_out,
       not_88_out, not_89_out, not_90_out, not_91_out, not_92_out, not_93_out, not_94_out, not_95_out,
       not_96_out, not_97_out, not_98_out, not_99_out, not_100_out, not_101_out, not_102_out, not_103_out,
       not_104_out, not_105_out, not_106_out, not_107_out, not_108_out, not_109_out, not_110_out,
       not_111_out, not_112_out, not_113_out, not_114_out, not_115_out, not_116_out, not_117_out,
       not_118_out, not_119_out, not_120_out, not_121_out, not_122_out, not_123_out, not_124_out,
       not_125_out, not_126_out, not_127_out, not_128_out, not_129_out, not_130_out, not_131_out,
       not_132_out, not_133_out, not_134_out, not_135_out, not_136_out, or_1_out, or_2_out;

  not not_1 (not_1_out, Funct1);
  not not_2 (not_2_out, Funct2);
  not not_3 (not_3_out, Funct3);
  not not_4 (not_4_out, Funct4);
  not not_5 (not_5_out, Funct5);
  not not_6 (not_6_out, Funct1);
  not not_7 (not_7_out, Funct2);
  not not_8 (not_8_out, Funct4);
  not not_9 (not_9_out, Funct5);
  not not_10 (not_10_out, Funct1);
  not not_11 (not_11_out, Funct2);
  not not_12 (not_12_out, Funct3);
  not not_13 (not_13_out, Funct4);
  not not_14 (not_14_out, Funct1);
  not not_15 (not_15_out, Funct2);
  not not_16 (not_16_out, Funct3);
  not not_17 (not_17_out, Funct5);
  not not_18 (not_18_out, Funct1);
  not not_19 (not_19_out, Funct2);
  not not_20 (not_20_out, Funct4);
  not not_21 (not_21_out, Funct1);
  not not_22 (not_22_out, Funct2);
  not not_23 (not_23_out, Funct1);
  not not_24 (not_24_out, Funct3);
  not not_25 (not_25_out, Funct5);
  not not_26 (not_26_out, Funct1);
  not not_27 (not_27_out, Funct3);
  not not_28 (not_28_out, Funct0);
  not not_29 (not_29_out, Funct1);
  not not_30 (not_30_out, Funct3);
  not not_31 (not_31_out, Funct4);
  not not_32 (not_32_out, Funct5);
  not not_33 (not_33_out, Funct1);
  not not_34 (not_34_out, Funct2);
  not not_35 (not_35_out, Funct3);
  not not_36 (not_36_out, Funct4);
  not not_37 (not_37_out, Funct5);
  not not_38 (not_38_out, Funct1);
  not not_39 (not_39_out, Funct2);
  not not_40 (not_40_out, Funct3);
  not not_41 (not_41_out, Funct4);
  not not_42 (not_42_out, Funct1);
  not not_43 (not_43_out, Funct2);
  not not_44 (not_44_out, Funct4);
  not not_45 (not_45_out, Funct5);
  not not_46 (not_46_out, Funct0);
  not not_47 (not_47_out, Funct1);
  not not_48 (not_48_out, Funct2);
  not not_49 (not_49_out, Funct3);
  not not_50 (not_50_out, Funct4);
  not not_51 (not_51_out, Funct5);
  not not_52 (not_52_out, Funct0);
  not not_53 (not_53_out, Funct1);
  not not_54 (not_54_out, Funct2);
  not not_55 (not_55_out, Funct3);
  not not_56 (not_56_out, Funct0);
  not not_57 (not_57_out, Funct1);
  not not_58 (not_58_out, Funct2);
  not not_59 (not_59_out, Funct3);
  not not_60 (not_60_out, Funct5);
  not not_61 (not_61_out, Funct1);
  not not_62 (not_62_out, Funct2);
  not not_63 (not_63_out, Funct3);
  not not_64 (not_64_out, Funct5);
  not not_65 (not_65_out, Funct1);
  not not_66 (not_66_out, Funct2);
  not not_67 (not_67_out, Funct4);
  not not_68 (not_68_out, Funct1);
  not not_69 (not_69_out, Funct2);
  not not_70 (not_70_out, Funct1);
  not not_71 (not_71_out, Funct3);
  not not_72 (not_72_out, Funct5);
  not not_73 (not_73_out, Funct1);
  not not_74 (not_74_out, Funct3);
  and and_1 (and_1_out, Funct0, not_1_out, not_2_out, not_3_out, not_4_out, not_5_out);
  and and_2 (and_2_out, Funct0, not_6_out, not_7_out, Funct3, not_8_out, not_9_out);
  and and_3 (and_3_out, Funct0, not_10_out, not_11_out, not_12_out, not_13_out, Funct5);
  and and_4 (and_4_out, Funct0, not_14_out, not_15_out, not_16_out, Funct4, not_17_out);
  and and_5 (and_5_out, Funct0, not_18_out, not_19_out, Funct3, not_20_out, Funct5);
  and and_6 (and_6_out, Funct0, not_21_out, not_22_out, Funct3, Funct4, Funct5);
  and and_7 (and_7_out, Funct0, not_23_out, Funct2, not_24_out, Funct4, not_25_out);
  and and_8 (and_8_out, Funct0, not_26_out, Funct2, not_27_out, Funct4, Funct5);
  and and_9 (and_9_out, not_28_out, not_29_out, Funct2, not_30_out, not_31_out, not_32_out);
  and and_10 (and_10_out, Funct0, not_33_out, not_34_out, not_35_out, not_36_out, not_37_out);
  and and_11 (and_11_out, Funct0, not_38_out, not_39_out, not_40_out, not_41_out, Funct5);
  and and_12 (and_12_out, Funct0, not_42_out, not_43_out, Funct3, not_44_out, not_45_out);
  and and_13 (and_13_out, not_46_out, not_47_out, not_48_out, not_49_out, not_50_out, not_51_out);
  and and_14 (and_14_out, not_52_out, not_53_out, not_54_out, not_55_out, Funct4, Funct5);
  and and_15 (and_15_out, not_56_out, not_57_out, not_58_out, not_59_out, Funct4, not_60_out);
  and and_16 (and_16_out, Funct0, not_61_out, not_62_out, not_63_out, Funct4, not_64_out);
  and and_17 (and_17_out, Funct0, not_65_out, not_66_out, Funct3, not_67_out, Funct5);
  and and_18 (and_18_out, Funct0, not_68_out, not_69_out, Funct3, Funct4, Funct5);
  and and_19 (and_19_out, Funct0, not_70_out, Funct2, not_71_out, Funct4, not_72_out);
  and and_20 (and_20_out, Funct0, not_73_out, Funct2, not_74_out, Funct4, Funct5);
  not not_75 (not_75_out, op0);
  not not_76 (not_76_out, op1);
  not not_77 (not_77_out, op2);
  not not_78 (not_78_out, op3);
  not not_79 (not_79_out, op4);
  not not_80 (not_80_out, op5);
  or or_1 (or_1_out, and_1_out, and_2_out, and_3_out, and_4_out, and_5_out, and_6_out, and_7_out, and_8_out, and_9_out);
  not not_81 (not_81_out, op0);
  not not_82 (not_82_out, op1);
  not not_83 (not_83_out, op3);
  not not_84 (not_84_out, op4);
  not not_85 (not_85_out, op5);
  not not_86 (not_86_out, op0);
  not not_87 (not_87_out, op1);
  not not_88 (not_88_out, op3);
  not not_89 (not_89_out, op4);
  not not_90 (not_90_out, op0);
  not not_91 (not_91_out, op1);
  not not_92 (not_92_out, op4);
  not not_93 (not_93_out, op5);
  not not_94 (not_94_out, op0);
  not not_95 (not_95_out, op1);
  not not_96 (not_96_out, op4);
  not not_97 (not_97_out, op1);
  not not_98 (not_98_out, op2);
  not not_99 (not_99_out, op3);
  not not_100 (not_100_out, op0);
  not not_101 (not_101_out, op1);
  not not_102 (not_102_out, op2);
  not not_103 (not_103_out, op4);
  not not_104 (not_104_out, op5);
  not not_105 (not_105_out, op0);
  not not_106 (not_106_out, op1);
  not not_107 (not_107_out, op2);
  not not_108 (not_108_out, op4);
  not not_109 (not_109_out, op0);
  not not_110 (not_110_out, op1);
  not not_111 (not_111_out, op3);
  not not_112 (not_112_out, op5);
  not not_113 (not_113_out, op1);
  not not_114 (not_114_out, op3);
  not not_115 (not_115_out, op0);
  not not_116 (not_116_out, op1);
  not not_117 (not_117_out, op2);
  not not_118 (not_118_out, op3);
  not not_119 (not_119_out, op4);
  not not_120 (not_120_out, op5);
  or or_2 (or_2_out, and_10_out, and_11_out, and_12_out, and_13_out, and_14_out, and_15_out, and_16_out, and_17_out, and_18_out, and_19_out, and_20_out);
  not not_121 (not_121_out, op0);
  not not_122 (not_122_out, op1);
  not not_123 (not_123_out, op2);
  not not_124 (not_124_out, op4);
  not not_125 (not_125_out, op5);
  not not_126 (not_126_out, op0);
  not not_127 (not_127_out, op1);
  not not_128 (not_128_out, op2);
  not not_129 (not_129_out, op4);
  not not_130 (not_130_out, op0);
  not not_131 (not_131_out, op2);
  not not_132 (not_132_out, op3);
  not not_133 (not_133_out, op4);
  not not_134 (not_134_out, op5);
  not not_135 (not_135_out, op1);
  not not_136 (not_136_out, op3);
  and and_21 (and_21_out, not_75_out, not_76_out, not_77_out, not_78_out, not_79_out, not_80_out, or_1_out);
  and and_22 (and_22_out, not_81_out, not_82_out, op2, not_83_out, not_84_out, not_85_out);
  and and_23 (and_23_out, not_86_out, not_87_out, op2, not_88_out, not_89_out, op5);
  and and_24 (and_24_out, not_90_out, not_91_out, op2, op3, not_92_out, not_93_out);
  and and_25 (and_25_out, not_94_out, not_95_out, op2, op3, not_96_out, op5);
  and and_26 (and_26_out, op0, not_97_out, not_98_out, not_99_out, op4, op5);
  and and_27 (and_27_out, not_100_out, not_101_out, not_102_out, op3, not_103_out, not_104_out);
  and and_28 (and_28_out, not_105_out, not_106_out, not_107_out, op3, not_108_out, op5);
  and and_29 (and_29_out, not_109_out, not_110_out, op2, not_111_out, op4, not_112_out);
  and and_30 (and_30_out, op0, not_113_out, op2, not_114_out, op4, op5);
  and and_31 (and_31_out, not_115_out, not_116_out, not_117_out, not_118_out, not_119_out, not_120_out, or_2_out);
  and and_32 (and_32_out, not_121_out, not_122_out, not_123_out, op3, not_124_out, not_125_out);
  and and_33 (and_33_out, not_126_out, not_127_out, not_128_out, op3, not_129_out, op5);
  and and_34 (and_34_out, not_130_out, op1, not_131_out, not_132_out, not_133_out, not_134_out);
  and and_35 (and_35_out, op0, not_135_out, op2, not_136_out, op4, op5);
  or or_3 (ReadRs, and_21_out, and_22_out, and_23_out, and_24_out, and_25_out, and_26_out, and_27_out, and_28_out, and_29_out, and_30_out);
  or or_4 (ReadRt, and_31_out, and_32_out, and_33_out, and_34_out, and_35_out);
endmodule
