// Logisim project pipeline.circ as structural Verilog: 4 circuits, main circuit IF/ID
module IF_ID (
  input  clk,
  input  clr,
  input  [31:0] instru_IF,
  input  [31:0] PCP4IF,
  input  En,
  output [31:0] InstruID,
  output [31:0] PCP4ID
);

  Register #(.width(32), .trigger("rising"), .Select("low")) register_1 (
    .D(instru_IF), .en(En), .Q(InstruID), .clk(clk), .clr(clr));
  Register #(.width(32), .trigger("rising"), .Select("low")) register_2 (
    .D(PCP4IF), .en(En), .Q(PCP4ID), .clk(clk), .clr(clr));
endmodule

module ID_EX (
  input  clk,
  input  clr,
  input  MemWriteID,
  input  [31:0] ImmID,
  input  IsJALID,
  input  JumpID,
  input  IsShamtID,
  input  [31:0] R1ID,
  input  BranchID,
  input  MemtoRegID,
  input  IsJRID,
  input  RegWriteID,
  input  [31:0] R2ID,
  input  IsSyscallID,
  input  BneOrBeqID,
  input  [3:0] ALUopID,
  input  ALUSrcID,
  input  [31:0] CP0Dout,
  input  [4:0] WriteReg_ID,
  input  IsExceptionID,
  input  [31:0] ShamtID,
  input  MemReadID,
  input  IsEret,
  input  [31:0] JumpAddr,
  input  [31:0] PCPlus4ID,
  input  En,
  output MemWriteEX,
  output [31:0] ImmEX,
  output IsJALEX,
  output JumpEX,
  output IsShamtEX,
  output [31:0] R1EX,
  output BranchEX,
  output MemtoRegEX,
  output IsJREX,
  output RegWriteEX,
  output [31:0] R2EX,
  output IsSyscallEX,
  output BneOrBeqEX,
  output [3:0] ALUopEX,
  output ALUSrcEX,
  output [31:0] CP0Dout_2,
  output [4:0] WriteReg_EX,
  output IsExceptionEX,
  output [31:0] ShamtEX,
  output MemReadEX,
  output IsEret_2,
  output [31:0] JumpAddr_2,
  output [31:0] PCPlusEX
);

  Register #(.width(32), .trigger("rising"), .Select("low")) register_1 (
    .D(ImmID), .en(En), .Q(ImmEX), .clk(clk), .clr(clr));
  Register #(.width(32), .trigger("rising"), .Select("low")) register_2 (
    .D(R1ID), .en(En), .Q(R1EX), .clk(clk), .clr(clr));
  Register #(.width(32), .trigger("rising"), .Select("low")) register_3 (
    .D(R2ID), .en(En), .Q(R2EX), .clk(clk), .clr(clr));
  Register #(.width(32), .trigger("rising"), .Select("low")) register_4 (
    .D(CP0Dout), .en(En), .Q(CP0Dout_2), .clk(clk), .clr(clr));
  Register #(.width(32), .trigger("rising"), .Select("low")) register_5 (
    .D(ShamtID), .en(En), .Q(ShamtEX), .clk(clk), .clr(clr));
  Register #(.width(32), .trigger("rising"), .Select("low")) register_6 (
    .D(JumpAddr), .en(En), .Q(JumpAddr_2), .clk(clk), .clr(clr));
  Register #(.width(32), .trigger("rising"), .Select("low")) register_7 (
    .D(PCPlus4ID), .en(En), .Q(PCPlusEX), .clk(clk), .clr(clr));
  Register #(.width(1), .trigger("rising"), .Select("low")) register_8 (
    .D(IsJALID), .en(En), .Q(IsJALEX), .clk(clk), .clr(clr));
  Register #(.width(1), .trigger("rising"), .Select("low")) register_9 (
    .D(IsShamtID), .en(En), .Q(IsShamtEX), .clk(clk), .clr(clr));
  Register #(.width(1), .trigger("rising"), .Select("low")) register_10 (
    .D(MemtoRegID), .en(En), .Q(MemtoRegEX), .clk(clk), .clr(clr));
  Register #(.width(1), .trigger("rising"), .Select("low")) register_11 (
    .D(RegWriteID), .en(En), .Q(RegWriteEX), .clk(clk), .clr(clr));
  Register #(.width(1), .trigger("rising"), .Select("low")) register_12 (
    .D(BneOrBeqID), .en(En), .Q(BneOrBeqEX), .clk(clk), .clr(clr));
  Register #(.width(1), .trigger("rising"), .Select("low")) register_13 (
    .D(ALUSrcID), .en(En), .Q(ALUSrcEX), .clk(clk), .clr(clr));
  Register #(.width(1), .trigger("rising"), .Select("low")) register_14 (
    .D(IsExceptionID), .en(En), .Q(IsExceptionEX), .clk(clk), .clr(clr));
  Register #(.width(1), .trigger("rising"), .Select("low")) register_15 (
    .D(MemReadID), .en(En), .Q(MemReadEX), .clk(clk), .clr(clr));
  Register #(.width(1), .trigger("rising"), .Select("low")) register_16 (
    .D(MemWriteID), .en(En), .Q(MemWriteEX), .clk(clk), .clr(clr));
  Register #(.width(1), .trigger("rising"), .Select("low")) register_17 (
    .D(JumpID), .en(En), .Q(JumpEX), .clk(clk), .clr(clr));
  Register #(.width(1), .trigger("rising"), .Select("low")) register_18 (
    .D(BranchID), .en(En), .Q(BranchEX), .clk(clk), .clr(clr));
  Register #(.width(1), .trigger("rising"), .Select("low")) register_19 (
    .D(IsJRID), .en(En), .Q(IsJREX), .clk(clk), .clr(clr));
  Register #(.width(1), .trigger("rising"), .Select("low")) register_20 (
    .D(IsSyscallID), .en(En), .Q(IsSyscallEX), .clk(clk), .clr(clr));
  Register #(.width(4), .trigger("rising"), .Select("low")) register_21 (
    .D(ALUopID), .en(En), .Q(ALUopEX), .clk(clk), .clr(clr));
  Register #(.width(5), .trigger("rising"), .Select("low")) register_22 (
    .D(WriteReg_ID), .en(En), .Q(WriteReg_EX), .clk(clk), .clr(clr));
  Register #(.width(1), .trigger("rising"), .Select("low")) register_23 (
    .D(IsEret), .en(En), .Q(IsEret_2), .clk(clk), .clr(clr));
endmodule

module EX_MEM (
  input  clk,
  input  clr,
  input  IsJALEX,
  input  [31:0] ALUResultEX,
  input  MemtoRegEX,
  input  RegWriteEX,
  input  [31:0] WriteDataEX,
  input  IsExceptionEX,
  input  MemReadEX,
  input  [31:0] JumpAddrEX,
  input  MemWriteEX,
  input  [31:0] CP0Dout,
  input  IsSyscallEX,
  input  [4:0] WriteReg_EX,
  input  En,
  output IsJALMEM,
  output [31:0] ALUResultMEM,
  output MemtoRegMEM,
  output RegWriteMEM,
  output [31:0] WriteDataMEM,
  output IsExceptionMEM,
  output MemReadMEM,
  output [31:0] JumpAddrMEM,
  output MemWriteMEM,
  output [31:0] CP0Dout_2,
  output IsSyscallMEM,
  output [4:0] WriteReg_MEM
);

  Register #(.width(32), .trigger("rising"), .Select("low")) register_1 (
    .D(ALUResultEX), .en(En), .Q(ALUResultMEM), .clk(clk), .clr(clr));
  Register #(.width(32), .trigger("rising"), .Select("low")) register_2 (
    .D(WriteDataEX), .en(En), .Q(WriteDataMEM), .clk(clk), .clr(clr));
  Register #(.width(32), .trigger("rising"), .Select("low")) register_3 (
    .D(JumpAddrEX), .en(En), .Q(JumpAddrMEM), .clk(clk), .clr(clr));
  Register #(.width(32), .trigger("rising"), .Select("low")) register_4 (
    .D(CP0Dout), .en(En), .Q(CP0Dout_2), .clk(clk), .clr(clr));
  Register #(.width(1), .trigger("rising"), .Select("low")) register_5 (
    .D(IsJALEX), .en(En), .Q(IsJALMEM), .clk(clk), .clr(clr));
  Register #(.width(1), .trigger("rising"), .Select("low")) register_6 (
    .D(MemtoRegEX), .en(En), .Q(MemtoRegMEM), .clk(clk), .clr(clr));
  Register #(.width(1), .trigger("rising"), .Select("low")) register_7 (
    .D(RegWriteEX), .en(En), .Q(RegWriteMEM), .clk(clk), .clr(clr));
  Register #(.width(1), .trigger("rising"), .Select("low")) register_8 (
    .D(IsExceptionEX), .en(En), .Q(IsExceptionMEM), .clk(clk), .clr(clr));
  Register #(.width(1), .trigger("rising"), .Select("low")) register_9 (
    .D(MemReadEX), .en(En), .Q(MemReadMEM), .clk(clk), .clr(clr));
  Register #(.width(1), .trigger("rising"), .Select("low")) register_10 (
    .D(MemWriteEX), .en(En), .Q(MemWriteMEM), .clk(clk), .clr(clr));
  Register #(.width(1), .trigger("rising"), .Select("low")) register_11 (
    .D(IsSyscallEX), .en(En), .Q(IsSyscallMEM), .clk(clk), .clr(clr));
  Register #(.width(5), .trigger("rising"), .Select("low")) register_12 (
    .D(WriteReg_EX), .en(En), .Q(WriteReg_MEM), .clk(clk), .clr(clr));
endmodule

// MEM/WBN
module MEM_WB (
  input  clk,
  input  clr,
  input  IsJALMEM,
  input  MemtoRegMEM,
  input  RegWriteMEM,
  input  IsExceptionMEM,
  input  IsSyscallMEM,
  input  [4:0] WriteReg_MEM,
  input  [31:0] ALUResultMEM,
  input  [31:0] ReadDataMEM,
  input  [31:0] JumpAddrMEM,
  input  [31:0] JumpAddrMEM_2,
  input  En,
  output IsJALWB,
  output MemtoRegWB,
  output RegWriteWB,
  output IsExceptionWB,
  output IsSyscallWB,
  output [4:0] WriteReg_WB,
  output [31:0] ALUResultWB,
  output [31:0] ReadDataWB,
  output [31:0] JumpAddrWB,
  output [31:0] JumpAddrWB_2
);

  Register #(.width(1), .trigger("rising"), .Select("low")) register_1 (
    .D(IsJALMEM), .en(En), .Q(IsJALWB), .clk(clk), .clr(clr));
  Register #(.width(1), .trigger("rising"), .Select("low")) register_2 (
    .D(MemtoRegMEM), .en(En), .Q(MemtoRegWB), .clk(clk), .clr(clr));
  Register #(.width(1), .trigger("rising"), .Select("low")) register_3 (
    .D(RegWriteMEM), .en(En), .Q(RegWriteWB), .clk(clk), .clr(clr));
  Register #(.width(1), .trigger("rising"), .Select("low")) register_4 (
    .D(IsExceptionMEM), .en(En), .Q(IsExceptionWB), .clk(clk), .clr(clr));
  Register #(.width(1), .trigger("rising"), .Select("low")) register_5 (
    .D(IsSyscallMEM), .en(En), .Q(IsSyscallWB), .clk(clk), .clr(clr));
  Register #(.width(5), .trigger("rising"), .Select("low")) register_6 (
    .D(WriteReg_MEM), .en(En), .Q(WriteReg_WB), .clk(clk), .clr(clr));
  Register #(.width(32), .trigger("rising"), .Select("low")) register_7 (
    .D(ALUResultMEM), .en(En), .Q(ALUResultWB), .clk(clk), .clr(clr));
  Register #(.width(32), .trigger("rising"), .Select("low")) register_8 (
    .D(ReadDataMEM), .en(En), .Q(ReadDataWB), .clk(clk), .clr(clr));
  Register #(.width(32), .trigger("rising"), .Select("low")) register_9 (
    .D(JumpAddrMEM), .en(En), .Q(JumpAddrWB), .clk(clk), .clr(clr));
  Register #(.width(32), .trigger("rising"), .Select("low")) register_10 (
    .D(JumpAddrMEM_2), .en(En), .Q(JumpAddrWB_2), .clk(clk), .clr(clr));
endmodule
