// Logisim project pipeline.circ as structural Verilog: 3 circuits, main circuit main
module main (
);

  wire alu_1_p3, and_1_out, clk, clock_1_out, control_1_alusrc, control_1_bneorbeq, control_1_branch,
       control_1_iscop0, control_1_isjal, control_1_isjr, control_1_isshamt, control_1_issyscall,
       control_1_jump, control_1_memread, control_1_memtoreg, control_1_memwrite, control_1_readrs,
       control_1_readrt, control_1_regwrite, ex_mem_1_isexceptionmem, ex_mem_1_isjalmem,
       ex_mem_1_issyscallmem, ex_mem_1_memreadmem, ex_mem_1_memtoregmem, ex_mem_1_memwritemem, Halt,
       hazard_unit_1_flushid, hazard_unit_1_flushif, hazard_unit_1_stallid, hazard_unit_1_stallif,
       id_ex_1_alusrcex, id_ex_1_bneorbeqex, id_ex_1_branchex, id_ex_1_isexceptionex, id_ex_1_isjalex,
       id_ex_1_isjrex, id_ex_1_isshamtex, id_ex_1_issyscallex, id_ex_1_jumpex, id_ex_1_memreadex,
       id_ex_1_memtoregex, id_ex_1_memwriteex, mem_wb_1_isexceptionwb, mem_wb_1_isjalwb,
       mem_wb_1_issyscallwb, mem_wb_1_memtoregwb, not_1_out, not_2_out, or_1_out, RegDstID, regfile_1_p7,
       regfile_1_p8, RegWriteEX, RegWriteMEM, xor_1_out, ZeroExtendID;
  wire [3:0] control_1_aluop, id_ex_1_aluopex;
  wire [4:0] ex_mem_1_writereg_mem, id_ex_1_writereg_ex, multiplexer_5_out, multiplexer_6_out, regfile_1_p3;
  wire [31:0] a0, adder_1_out, adder_2_out, alu_1_p5, bit_extender_1_out, counter_1_q, ex_mem_1_aluresultmem,
       ex_mem_1_jumpaddrmem, ex_mem_1_writedatamem, hazard_unit_1_bubblenum, id_ex_1_immex,
       id_ex_1_jumpaddr_2, id_ex_1_pcplusex, id_ex_1_r1ex, id_ex_1_r2ex, id_ex_1_shamtex, if_id_1_instruid,
       if_id_1_pcp4id, immediate_extender_1_p3, mem_wb_1_aluresultwb, mem_wb_1_jumpaddrwb,
       mem_wb_1_jumpaddrwb_2, multiplexer_1_out, multiplexer_2_out, multiplexer_3_out, multiplexer_7_out,
       multiplexer_8_out, multiplexer_9_out, multiplexer_10_out, PC_q, ram_1_data, regfile_1_p4,
       regfile_1_p9, regfile_1_p10, rom_1_data, shifter_1_out, v0;

  Multiplexer #(.select(1), .width(32), .disabled("Z"), .enable("false")) multiplexer_1 (
    .in0(adder_1_out), .in1(adder_2_out), .out(multiplexer_1_out), .sel(and_1_out));
  Multiplexer #(.select(1), .width(32), .disabled("Z"), .enable("false")) multiplexer_2 (
    .in0(multiplexer_1_out), .in1(id_ex_1_jumpaddr_2), .out(multiplexer_2_out), .sel(id_ex_1_jumpex));
  Counter #(.width(32), .max('hffffffff), .ongoal("wrap"), .trigger("rising"), .behavior("old")) counter_1 (
    .count(and_1_out), .Q(counter_1_q), .clk(clk));  // open: load, D, carry, clr, preset
  Multiplexer #(.select(1), .width(32), .disabled("Z"), .enable("false")) multiplexer_3 (
    .in0(multiplexer_2_out), .in1(id_ex_1_r1ex), .out(multiplexer_3_out), .sel(id_ex_1_isjrex));
  Hazard_Unit hazard_unit_1 (
    .clk(clk), .FlushIF(hazard_unit_1_flushif), .FlushID(hazard_unit_1_flushid), .IsToBranchOrJump(or_1_out),
    .WriteReg_MEM(ex_mem_1_writereg_mem), .RT(if_id_1_instruid[20:16]), .RegWriteMEM(RegWriteMEM),
    .RS(if_id_1_instruid[25:21]), .StallIF(hazard_unit_1_stallif), .StallID(hazard_unit_1_stallid),
    .WriteReg_EX(id_ex_1_writereg_ex), .RegWriteEX(RegWriteEX), .ReadRs(control_1_readrs),
    .ReadRt(control_1_readrt), .BubbleNum(hazard_unit_1_bubblenum));
  // Probe on counter_1_q
  not not_1 (not_1_out, hazard_unit_1_stallif);
  Register #(.width(32), .trigger("rising"), .Select("low")) PC (
    .D(multiplexer_3_out), .en(not_1_out), .Q(PC_q), .clk(clk));  // open: clr
  Clock #(.highDuration(1), .lowDuration(1)) clock_1 (.out(clock_1_out));
  Adder #(.width(32)) adder_1 (.a(PC_q), .b(32'h4), .out(adder_1_out));  // open: cin, cout
  Multiplexer #(.select(1), .width(1), .disabled("Z"), .enable("false")) multiplexer_4 (
    .in0(clock_1_out), .in1(1'b0), .out(clk), .sel(Halt));
  // Probe on hazard_unit_1_bubblenum
  ROM #(.addrWidth(10), .dataWidth(32), .Select("high")) rom_1 (.addr(PC_q[11:2]), .data(rom_1_data));
  IF_ID if_id_1 (
    .instru_IF(rom_1_data), .InstruID(if_id_1_instruid), .clk(clk), .En(not_2_out),
    .clr(hazard_unit_1_flushif), .PCP4IF(adder_1_out), .PCP4ID(if_id_1_pcp4id));
  not not_2 (not_2_out, hazard_unit_1_stallid);
  Control control_1 (
    .op(if_id_1_instruid[31:26]), .Funct(if_id_1_instruid[5:0]), .ALUop(control_1_aluop),
    .IsJAL(control_1_isjal), .IsShamt(control_1_isshamt), .MemtoReg(control_1_memtoreg),
    .RegWrite(control_1_regwrite), .MemRead(control_1_memread), .MemWrite(control_1_memwrite),
    .Jump(control_1_jump), .Branch(control_1_branch), .RegDst(RegDstID), .BneOrBeq(control_1_bneorbeq),
    .ALUSrc(control_1_alusrc), .IsJR(control_1_isjr), .IsSyscall(control_1_issyscall),
    .IsCOP0(control_1_iscop0), .ZeroExtend(ZeroExtendID), .ReadRs(control_1_readrs), .ReadRt(control_1_readrt));
  // Immediate_Extender immediate_extender_1: pin names not known; wires that end beside it: if_id_1_instruid[15:0], ZeroExtendID, immediate_extender_1_p3
  Multiplexer #(.select(1), .width(5), .disabled("Z"), .enable("false")) multiplexer_5 (
    .in0(if_id_1_instruid[20:16]), .in1(if_id_1_instruid[15:11]), .out(multiplexer_5_out), .sel(RegDstID));
  // Regfile regfile_1: pin names not known; wires that end beside it: if_id_1_instruid[25:21], if_id_1_instruid[20:16], regfile_1_p3, regfile_1_p4, v0, a0, regfile_1_p7, regfile_1_p8, regfile_1_p9, regfile_1_p10
  Multiplexer #(.select(1), .width(5), .disabled("Z"), .enable("false")) multiplexer_6 (
    .in0(multiplexer_5_out), .in1({5{1'b1}}), .out(multiplexer_6_out), .sel(control_1_isjal));
  not not_3 (regfile_1_p7, clk);
  assign bit_extender_1_out = {{27{1'b0}}, if_id_1_instruid[10:6]};  // Bit_Extender bit_extender_1
  ID_EX id_ex_1 (
    .clk(clk), .IsJALID(control_1_isjal), .MemReadID(control_1_memread), .IsShamtID(control_1_isshamt),
    .MemWriteID(control_1_memwrite), .MemtoRegID(control_1_memtoreg), .JumpID(control_1_jump),
    .RegWriteID(control_1_regwrite), .BranchID(control_1_branch), .BneOrBeqID(control_1_bneorbeq),
    .ALUSrcID(control_1_alusrc), .IsJRID(control_1_isjr), .IsExceptionID(control_1_iscop0),
    .IsJALEX(id_ex_1_isjalex), .MemReadEX(id_ex_1_memreadex), .IsShamtEX(id_ex_1_isshamtex),
    .MemWriteEX(id_ex_1_memwriteex), .MemtoRegEX(id_ex_1_memtoregex), .JumpEX(id_ex_1_jumpex),
    .RegWriteEX(RegWriteEX), .BranchEX(id_ex_1_branchex), .BneOrBeqEX(id_ex_1_bneorbeqex),
    .ALUSrcEX(id_ex_1_alusrcex), .IsJREX(id_ex_1_isjrex), .IsExceptionEX(id_ex_1_isexceptionex),
    .ALUopID(control_1_aluop), .ALUopEX(id_ex_1_aluopex), .WriteReg_ID(multiplexer_6_out),
    .WriteReg_EX(id_ex_1_writereg_ex), .ImmID(immediate_extender_1_p3), .ImmEX(id_ex_1_immex),
    .R1ID(regfile_1_p9), .R1EX(id_ex_1_r1ex), .R2ID(regfile_1_p10), .R2EX(id_ex_1_r2ex),
    .PCPlus4ID(if_id_1_pcp4id), .PCPlusEX(id_ex_1_pcplusex), .ShamtID(bit_extender_1_out),
    .ShamtEX(id_ex_1_shamtex), .JumpAddr({if_id_1_pcp4id[31:28], if_id_1_instruid[25:0], 2'b00}),
    .JumpAddr_2(id_ex_1_jumpaddr_2), .IsSyscallID(control_1_issyscall), .IsSyscallEX(id_ex_1_issyscallex),
    .clr(hazard_unit_1_flushid), .En(1'b1));  // open: CP0Dout, CP0Dout_2, IsEret, IsEret_2
  Multiplexer #(.select(1), .width(32), .disabled("Z"), .enable("false")) multiplexer_7 (
    .in0(id_ex_1_r1ex), .in1(id_ex_1_r2ex), .out(multiplexer_7_out), .sel(id_ex_1_isshamtex));
  Multiplexer #(.select(1), .width(32), .disabled("Z"), .enable("false")) multiplexer_8 (
    .in0(id_ex_1_r2ex), .in1(id_ex_1_shamtex), .out(multiplexer_8_out), .sel(id_ex_1_isshamtex));
  Multiplexer #(.select(1), .width(32), .disabled("Z"), .enable("false")) multiplexer_9 (
    .in0(multiplexer_8_out), .in1(id_ex_1_immex), .out(multiplexer_9_out), .sel(id_ex_1_alusrcex));
  or or_1 (or_1_out, id_ex_1_isjalex, id_ex_1_isjrex, and_1_out, id_ex_1_jumpex);
  // ALU alu_1: pin names not known; wires that end beside it: multiplexer_7_out, multiplexer_9_out, alu_1_p3, id_ex_1_aluopex, alu_1_p5
  Shifter #(.width(32), .shift("ll")) shifter_1 (.in(id_ex_1_immex), .\dist (5'b00010), .out(shifter_1_out));
  EX_MEM ex_mem_1 (
    .MemReadEX(id_ex_1_memreadex), .MemReadMEM(ex_mem_1_memreadmem), .MemWriteEX(id_ex_1_memwriteex),
    .MemWriteMEM(ex_mem_1_memwritemem), .IsExceptionEX(id_ex_1_isexceptionex),
    .IsExceptionMEM(ex_mem_1_isexceptionmem), .IsJALEX(id_ex_1_isjalex), .IsJALMEM(ex_mem_1_isjalmem),
    .RegWriteEX(RegWriteEX), .RegWriteMEM(RegWriteMEM), .MemtoRegEX(id_ex_1_memtoregex),
    .MemtoRegMEM(ex_mem_1_memtoregmem), .clk(clk), .IsSyscallEX(id_ex_1_issyscallex),
    .IsSyscallMEM(ex_mem_1_issyscallmem), .ALUResultEX(alu_1_p5), .ALUResultMEM(ex_mem_1_aluresultmem),
    .WriteDataEX(id_ex_1_r2ex), .WriteDataMEM(ex_mem_1_writedatamem), .JumpAddrEX(id_ex_1_pcplusex),
    .JumpAddrMEM(ex_mem_1_jumpaddrmem), .WriteReg_EX(id_ex_1_writereg_ex),
    .WriteReg_MEM(ex_mem_1_writereg_mem), .clr(1'b0), .En(1'b1));  // open: CP0Dout, CP0Dout_2
  and and_1 (and_1_out, id_ex_1_branchex, xor_1_out);
  xor xor_1 (xor_1_out, id_ex_1_bneorbeqex, alu_1_p3);
  Adder #(.width(32)) adder_2 (.a(id_ex_1_pcplusex), .b(shifter_1_out), .out(adder_2_out));  // open: cin, cout
  RAM #(.addrWidth(10), .dataWidth(32), .bus("separate"), .Select("high")) ram_1 (
    .addr(ex_mem_1_aluresultmem[11:2]), .din(ex_mem_1_writedatamem), .data(ram_1_data),
    .str(ex_mem_1_memwritemem), .clk(clk), .ld(ex_mem_1_memreadmem));  // open: sel, clr
  MEM_WB mem_wb_1 (
    .IsJALMEM(ex_mem_1_isjalmem), .clk(clk), .MemtoRegMEM(ex_mem_1_memtoregmem), .RegWriteMEM(RegWriteMEM),
    .IsExceptionMEM(ex_mem_1_isexceptionmem), .IsJALWB(mem_wb_1_isjalwb), .MemtoRegWB(mem_wb_1_memtoregwb),
    .RegWriteWB(regfile_1_p8), .IsExceptionWB(mem_wb_1_isexceptionwb), .ALUResultMEM(ex_mem_1_aluresultmem),
    .ALUResultWB(mem_wb_1_aluresultwb), .JumpAddrMEM(ram_1_data), .JumpAddrWB(mem_wb_1_jumpaddrwb),
    .WriteReg_MEM(ex_mem_1_writereg_mem), .WriteReg_WB(regfile_1_p3), .IsSyscallMEM(ex_mem_1_issyscallmem),
    .IsSyscallWB(mem_wb_1_issyscallwb), .clr(1'b0), .En(1'b1), .JumpAddrMEM_2(ex_mem_1_jumpaddrmem),
    .JumpAddrWB_2(mem_wb_1_jumpaddrwb_2));  // open: ReadDataMEM, ReadDataWB
  // Syscall_Decoder syscall_decoder_1: pin names not known; wires that end beside it: mem_wb_1_isexceptionwb, v0, a0, clk, mem_wb_1_issyscallwb, Halt
  Multiplexer #(.select(1), .width(32), .disabled("Z"), .enable("false")) multiplexer_10 (
    .in0(mem_wb_1_aluresultwb), .in1(mem_wb_1_jumpaddrwb), .out(multiplexer_10_out), .sel(mem_wb_1_memtoregwb));
  Multiplexer #(.select(1), .width(32), .disabled("Z"), .enable("false")) multiplexer_11 (
    .in0(multiplexer_10_out), .in1(mem_wb_1_jumpaddrwb_2), .out(regfile_1_p4), .sel(mem_wb_1_isjalwb));

  // Notes on the sheet:
  //   取指
  //   contents of rom_1 (hex, n*v repeats v):
  //   20010001 10200004 10210003 0 0 0 2002000a c
  //   OP
  //   Funct
  //   RS
  //   RT
  //   RD
  //   IsJAL
  //   RegWrite
  //   MemToReg
  //   IsCOP0
  //   MemToReg
  //   MemRead
  //   IsJR
  //   Branch
  //   BB
  //   Jump
  //   ALUop
  //   ALUscr
  //   SHAM
  //   Sys
  //   译码
  //   JumpAddr
  //   Immediate
  //   PCPlus4ID
  //   JR Addr
  //   Jump Addr
  //   Branch Addr
  //   Shamt
  //   WriteReg#
  //   IsToBranchOrJump
  //   执行
  //   WriteDataEX
  //   访存
  //   WriteReg#MEM
  //   Ignored
  //   WriteReg#WB
  //   WB_DATA
  //   写回
endmodule

module Hazard_Unit (
  input  clk,
  input  ReadRs,
  input  ReadRt,
  input  [4:0] WriteReg_MEM,
  input  [4:0] RT,
  input  RegWriteMEM,
  input  RegWriteEX,
  input  [4:0] WriteReg_EX,
  input  [4:0] RS,
  input  IsToBranchOrJump,
  output FlushIF,
  output FlushID,
  output StallID,
  output StallIF,
  output [31:0] BubbleNum
);

  wire and_2_out, and_3_out, and_4_out, and_5_out, and_6_out, and_7_out, and_8_out, and_9_out,
       comparator_1_eq, comparator_2_eq, comparator_3_eq, comparator_4_eq, comparator_5_eq, comparator_6_eq,
       d_ff_1_q, d_ff_2_q, not_1_out, not_2_out, or_1_out, or_2_out;

  Comparator #(.width(5), .mode("twosComplement")) comparator_1 (
    .a({5{1'b0}}), .b(WriteReg_MEM), .eq(comparator_1_eq));  // open: gt, lt
  Comparator #(.width(5), .mode("twosComplement")) comparator_2 (
    .a(WriteReg_MEM), .b(RT), .eq(comparator_2_eq));  // open: gt, lt
  Comparator #(.width(5), .mode("twosComplement")) comparator_3 (
    .a(WriteReg_MEM), .b(RS), .eq(comparator_3_eq));  // open: gt, lt
  Comparator #(.width(5), .mode("twosComplement")) comparator_4 (
    .a({5{1'b0}}), .b(WriteReg_EX), .eq(comparator_4_eq));  // open: gt, lt
  Comparator #(.width(5), .mode("twosComplement")) comparator_5 (
    .a(WriteReg_EX), .b(RT), .eq(comparator_5_eq));  // open: gt, lt
  Comparator #(.width(5), .mode("twosComplement")) comparator_6 (
    .a(WriteReg_EX), .b(RS), .eq(comparator_6_eq));  // open: gt, lt
  Counter #(.width(32), .max('hffffffff), .ongoal("wrap"), .trigger("rising"), .behavior("old")) counter_1 (
    .count(StallID), .Q(BubbleNum), .clk(clk));  // open: load, D, carry, clr, preset
  not not_1 (not_1_out, comparator_1_eq);
  not not_2 (not_2_out, comparator_4_eq);
  and and_1 (FlushID, clk, d_ff_1_q);
  D_Flip_Flop #(.trigger("falling"), .Pre_Clr_Positions("LEGACY"), .NegatePresetClear("false"), .enable("true"), .NewFFLayout("false")) d_ff_1 (
    .clk(clk), .D(StallID), .Q(d_ff_1_q));  // open: Qn, preset, en, reset
  and and_2 (and_2_out, ReadRt, comparator_2_eq);
  and and_3 (and_3_out, comparator_3_eq, ReadRs);
  and and_4 (and_4_out, ReadRt, comparator_5_eq);
  and and_5 (and_5_out, ReadRs, comparator_6_eq);
  or or_1 (or_1_out, and_2_out, and_3_out);
  or or_2 (or_2_out, and_4_out, and_5_out);
  and and_6 (and_6_out, not_1_out, or_1_out);
  and and_7 (and_7_out, not_2_out, or_2_out);
  and and_8 (and_8_out, RegWriteMEM, and_6_out);
  and and_9 (and_9_out, RegWriteEX, and_7_out);
  D_Flip_Flop #(.trigger("falling"), .Pre_Clr_Positions("LEGACY"), .NegatePresetClear("false"), .enable("true"), .NewFFLayout("false")) d_ff_2 (
    .clk(clk), .D(IsToBranchOrJump), .Q(d_ff_2_q));  // open: Qn, preset, en, reset
  or or_3 (StallID, and_8_out, and_9_out);
  and and_10 (FlushIF, ~clk, d_ff_2_q);  // AND_Gate

  assign StallIF = StallID;

  // Other names for the same wires on the sheet: RES = StallID
endmodule

module Hazard_Detector (
  input  op0,
  input  op1,
  input  op2,
  input  op3,
  input  op4,
  input  op5,
  input  Funct0,
  input  Funct1,
  input  Funct2,
  input  Funct3,
  input  Funct4,
  input  Funct5,
  output ReadRs,
  output ReadRt
);

  wire and_1_out, and_2_out, and_3_out, and_4_out, and_5_out, and_6_out, and_7_out, and_8_out, and_9_out,
       and_10_out, and_11_out, and_12_out, and_13_out, and_14_out, and_15_out, and_16_out, and_17_out,
       and_18_out, and_19_out, and_20_out, and_21_out, and_22_out, and_23_out, and_24_out, and_25_out,
       and_26_out, and_27_out, and_28_out, and_29_out, and_30_out, and_31_out, and_32_out, and_33_out,
       and_34_out, not_1_out, not_2_out, not_3_out, not_4_out, not_5_out, not_6_out, not_7_out, not_8_out,
       not_9_out, not_10_out, not_11_out, not_12_out, not_13_out, not_14_out, not_15_out, not_16_out,
       not_17_out, not_18_out, not_19_out, not_20_out, not_21_out, not_22_out, not_23_out, not_24_out,
       not_25_out, not_26_out, not_27_out, not_28_out, not_29_out, not_30_out, not_31_out, not_32_out,
       not_33_out, not_34_out, not_35_out, not_36_out, not_37_out, not_38_out, not_39_out, not_40_out,
       not_41_out, not_42_out, not_43_out, not_44_out, not_45_out, not_46_out, not_47_out, not_48_out,
       not_49_out, not_50_out, not_51_out, not_52_out, not_53_out, not_54_out, not_55_out, not_56_out,
       not_57_out, not_58_out, not_59_out, not_60_out, not_61_out, not_62_out, not_63_out, not_64_out,
       not_65_out, not_66_out, not_67_out, not_68_out, not_69_out, not_70_out, not_71_out, not_72_out,
       not_73_out, not_74_out, not_75_out, not_76_out, not_77_out, not_78_out, not_79_out, not_80_out,
       not_81_out, not_82_out, not_83_out, not_84_out, not_85_out, not_86_out, not_87_out, not_88_out,
       not_89_out, not_90_out, not_91_out, not_92_out, not_93_out, not_94_out, not_95_out, not_96_out,
       not_97_out, not_98_out, not_99_out, not_100_out, not_101_out, not_102_out, not_103_out, not_104_out,
       not_105_out, not_106_out, not_107_out, not_108_out, not_109_out, not_110_out, not_111_out,
       not_112_out, not_113_out, not_114_out, not_115_out, not_116_out, not_117_out, not_118_out,
       not_119_out, not_120_out, not_121_out, not_122_out, not_123_out, not_124_out, not_125_out,
       not_126_out, not_127_out, not_128_out, not_129_out, not_130_out, not_131_out, not_132_out,
       not_133_out, not_134_out, or_1_out, or_2_out;

  not not_1 (not_1_out, Funct1);
  not not_2 (not_2_out, Funct2);
  not not_3 (not_3_out, Funct3);
  not not_4 (not_4_out, Funct4);
  not not_5 (not_5_out, Funct5);
  not not_6 (not_6_out, Funct1);
  not not_7 (not_7_out, Funct2);
  not not_8 (not_8_out, Funct4);
  not not_9 (not_9_out, Funct5);
  not not_10 (not_10_out, Funct1);
  not not_11 (not_11_out, Funct2);
  not not_12 (not_12_out, Funct3);
  not not_13 (not_13_out, Funct4);
  not not_14 (not_14_out, Funct1);
  not not_15 (not_15_out, Funct2);
  not not_16 (not_16_out, Funct3);
  not not_17 (not_17_out, Funct5);
  not not_18 (not_18_out, Funct1);
  not not_19 (not_19_out, Funct2);
  not not_20 (not_20_out, Funct4);
  not not_21 (not_21_out, Funct1);
  not not_22 (not_22_out, Funct2);
  not not_23 (not_23_out, Funct1);
  not not_24 (not_24_out, Funct3);
  not not_25 (not_25_out, Funct5);
  not not_26 (not_26_out, Funct1);
  not not_27 (not_27_out, Funct3);
  not not_28 (not_28_out, Funct0);
  not not_29 (not_29_out, Funct1);
  not not_30 (not_30_out, Funct3);
  not not_31 (not_31_out, Funct4);
  not not_32 (not_32_out, Funct5);
  not not_33 (not_33_out, Funct1);
  not not_34 (not_34_out, Funct2);
  not not_35 (not_35_out, Funct3);
  not not_36 (not_36_out, Funct4);
  not not_37 (not_37_out, Funct5);
  not not_38 (not_38_out, Funct1);
  not not_39 (not_39_out, Funct2);
  not not_40 (not_40_out, Funct3);
  not not_41 (not_41_out, Funct4);
  not not_42 (not_42_out, Funct1);
  not not_43 (not_43_out, Funct2);
  not not_44 (not_44_out, Funct4);
  not not_45 (not_45_out, Funct5);
  not not_46 (not_46_out, Funct0);
  not not_47 (not_47_out, Funct1);
  not not_48 (not_48_out, Funct2);
  not not_49 (not_49_out, Funct3);
  not not_50 (not_50_out, Funct4);
  not not_51 (not_51_out, Funct5);
  not not_52 (not_52_out, Funct0);
  not not_53 (not_53_out, Funct1);
  not not_54 (not_54_out, Funct2);
  not not_55 (not_55_out, Funct3);
  not not_56 (not_56_out, Funct0);
  not not_57 (not_57_out, Funct1);
  not not_58 (not_58_out, Funct2);
  not not_59 (not_59_out, Funct3);
  not not_60 (not_60_out, Funct5);
  not not_61 (not_61_out, Funct1);
  not not_62 (not_62_out, Funct2);
  not not_63 (not_63_out, Funct3);
  not not_64 (not_64_out, Funct5);
  not not_65 (not_65_out, Funct1);
  not not_66 (not_66_out, Funct2);
  not not_67 (not_67_out, Funct4);
  not not_68 (not_68_out, Funct1);
  not not_69 (not_69_out, Funct2);
  not not_70 (not_70_out, Funct1);
  not not_71 (not_71_out, Funct3);
  not not_72 (not_72_out, Funct5);
  not not_73 (not_73_out, Funct1);
  not not_74 (not_74_out, Funct3);
  and and_1 (and_1_out, Funct0, not_1_out, not_2_out, not_3_out, not_4_out, not_5_out);
  and and_2 (and_2_out, Funct0, not_6_out, not_7_out, Funct3, not_8_out, not_9_out);
  and and_3 (and_3_out, Funct0, not_10_out, not_11_out, not_12_out, not_13_out, Funct5);
  and and_4 (and_4_out, Funct0, not_14_out, not_15_out, not_16_out, Funct4, not_17_out);
  and and_5 (and_5_out, Funct0, not_18_out, not_19_out, Funct3, not_20_out, Funct5);
  and and_6 (and_6_out, Funct0, not_21_out, not_22_out, Funct3, Funct4, Funct5);
  and and_7 (and_7_out, Funct0, not_23_out, Funct2, not_24_out, Funct4, not_25_out);
  and and_8 (and_8_out, Funct0, not_26_out, Funct2, not_27_out, Funct4, Funct5);
  and and_9 (and_9_out, not_28_out, not_29_out, Funct2, not_30_out, not_31_out, not_32_out);
  and and_10 (and_10_out, Funct0, not_33_out, not_34_out, not_35_out, not_36_out, not_37_out);
  and and_11 (and_11_out, Funct0, not_38_out, not_39_out, not_40_out, not_41_out, Funct5);
  and and_12 (and_12_out, Funct0, not_42_out, not_43_out, Funct3, not_44_out, not_45_out);
  and and_13 (and_13_out, not_46_out, not_47_out, not_48_out, not_49_out, not_50_out, not_51_out);
  and and_14 (and_14_out, not_52_out, not_53_out, not_54_out, not_55_out, Funct4, Funct5);
  and and_15 (and_15_out, not_56_out, not_57_out, not_58_out, not_59_out, Funct4, not_60_out);
  and and_16 (and_16_out, Funct0, not_61_out, not_62_out, not_63_out, Funct4, not_64_out);
  and and_17 (and_17_out, Funct0, not_65_out, not_66_out, Funct3, not_67_out, Funct5);
  and and_18 (and_18_out, Funct0, not_68_out, not_69_out, Funct3, Funct4, Funct5);
  and and_19 (and_19_out, Funct0, not_70_out, Funct2, not_71_out, Funct4, not_72_out);
  and and_20 (and_20_out, Funct0, not_73_out, Funct2, not_74_out, Funct4, Funct5);
  not not_75 (not_75_out, op0);
  not not_76 (not_76_out, op1);
  not not_77 (not_77_out, op2);
  not not_78 (not_78_out, op3);
  not not_79 (not_79_out, op4);
  not not_80 (not_80_out, op5);
  or or_1 (or_1_out, and_1_out, and_2_out, and_3_out, and_4_out, and_5_out, and_6_out, and_7_out, and_8_out, and_9_out);
  not not_81 (not_81_out, op0);
  not not_82 (not_82_out, op1);
  not not_83 (not_83_out, op3);
  not not_84 (not_84_out, op4);
  not not_85 (not_85_out, op5);
  not not_86 (not_86_out, op0);
  not not_87 (not_87_out, op1);
  not not_88 (not_88_out, op3);
  not not_89 (not_89_out, op4);
  not not_90 (not_90_out, op0);
  not not_91 (not_91_out, op1);
  not not_92 (not_92_out, op4);
  not not_93 (not_93_out, op5);
  not not_94 (not_94_out, op0);
  not not_95 (not_95_out, op1);
  not not_96 (not_96_out, op4);
  not not_97 (not_97_out, op1);
  not not_98 (not_98_out, op2);
  not not_99 (not_99_out, op3);
  not not_100 (not_100_out, op1);
  not not_101 (not_101_out, op3);
  not not_102 (not_102_out, op0);
  not not_103 (not_103_out, op1);
  not not_104 (not_104_out, op2);
  not not_105 (not_105_out, op4);
  not not_106 (not_106_out, op5);
  not not_107 (not_107_out, op0);
  not not_108 (not_108_out, op1);
  not not_109 (not_109_out, op2);
  not not_110 (not_110_out, op4);
  not not_111 (not_111_out, op0);
  not not_112 (not_112_out, op1);
  not not_113 (not_113_out, op3);
  not not_114 (not_114_out, op5);
  not not_115 (not_115_out, op0);
  not not_116 (not_116_out, op1);
  not not_117 (not_117_out, op2);
  not not_118 (not_118_out, op3);
  not not_119 (not_119_out, op4);
  not not_120 (not_120_out, op5);
  or or_2 (or_2_out, and_10_out, and_11_out, and_12_out, and_13_out, and_14_out, and_15_out, and_16_out, and_17_out, and_18_out, and_19_out, and_20_out);
  not not_121 (not_121_out, op0);
  not not_122 (not_122_out, op1);
  not not_123 (not_123_out, op2);
  not not_124 (not_124_out, op4);
  not not_125 (not_125_out, op5);
  not not_126 (not_126_out, op0);
  not not_127 (not_127_out, op1);
  not not_128 (not_128_out, op2);
  not not_129 (not_129_out, op4);
  not not_130 (not_130_out, op0);
  not not_131 (not_131_out, op2);
  not not_132 (not_132_out, op3);
  not not_133 (not_133_out, op4);
  not not_134 (not_134_out, op5);
  and and_21 (and_21_out, not_75_out, not_76_out, not_77_out, not_78_out, not_79_out, not_80_out, or_1_out);
  and and_22 (and_22_out, not_81_out, not_82_out, op2, not_83_out, not_84_out, not_85_out);
  and and_23 (and_23_out, not_86_out, not_87_out, op2, not_88_out, not_89_out, op5);
  and and_24 (and_24_out, not_90_out, not_91_out, op2, op3, not_92_out, not_93_out);
  and and_25 (and_25_out, not_94_out, not_95_out, op2, op3, not_96_out, op5);
  and and_26 (and_26_out, op0, not_97_out, not_98_out, not_99_out, op4, op5);
  and and_27 (and_27_out, op0, not_100_out, op2, not_101_out, op4, op5);
  and and_28 (and_28_out, not_102_out, not_103_out, not_104_out, op3, not_105_out, not_106_out);
  and and_29 (and_29_out, not_107_out, not_108_out, not_109_out, op3, not_110_out, op5);
  and and_30 (and_30_out, not_111_out, not_112_out, op2, not_113_out, op4, not_114_out);
  and and_31 (and_31_out, not_115_out, not_116_out, not_117_out, not_118_out, not_119_out, not_120_out, or_2_out);
  and and_32 (and_32_out, not_121_out, not_122_out, not_123_out, op3, not_124_out, not_125_out);
  and and_33 (and_33_out, not_126_out, not_127_out, not_128_out, op3, not_129_out, op5);
  and and_34 (and_34_out, not_130_out, op1, not_131_out, not_132_out, not_133_out, not_134_out);
  or or_3 (ReadRs, and_21_out, and_22_out, and_23_out, and_24_out, and_25_out, and_26_out, and_27_out, and_28_out, and_29_out, and_30_out);
  or or_4 (ReadRt, and_31_out, and_32_out, and_33_out, and_34_out);
endmodule
