// Logisim project quanjiaqi.circ as structural Verilog
module \半加器  (
  input  in_1,
  input  in_2,
  output out_3,
  output out_4
);

  xor xor_1 (out_4, in_1, in_2);
  and and_1 (out_3, in_1, in_2);
endmodule

module \全加器  (
  input  in_1,
  input  in_2,
  input  in_3,
  output out_4,
  output out_5
);

  wire \半加器_1_out_3 , \半加器_1_out_4 , \半加器_2_out_3 ;

  \半加器  \u_半加器_1  (.in_1(in_1), .in_2(in_2), .out_3(\半加器_1_out_3 ), .out_4(\半加器_1_out_4 ));
  \半加器  \u_半加器_2  (.in_1(\半加器_1_out_4 ), .in_2(in_3), .out_3(\半加器_2_out_3 ), .out_4(out_5));
  or or_1 (out_4, \半加器_2_out_3 , \半加器_1_out_3 );
endmodule

module \四位全加器  (
  input  [3:0] in_1,
  input  [3:0] in_2,
  input  in_3,
  output [3:0] out_4,
  output out_5
);

  wire \全加器_1_out_4 , \全加器_2_out_4 , \全加器_3_out_4 ;

  \全加器  \u_全加器_1  (.in_3(in_1[0]), .in_1(in_2[0]), .in_2(in_3), .out_5(out_4[0]), .out_4(\全加器_1_out_4 ));
  \全加器  \u_全加器_2  (.in_3(in_1[1]), .in_1(in_2[1]), .in_2(\全加器_1_out_4 ), .out_5(out_4[1]), .out_4(\全加器_2_out_4 ));
  \全加器  \u_全加器_3  (.in_3(in_1[2]), .in_1(in_2[2]), .in_2(\全加器_2_out_4 ), .out_5(out_4[2]), .out_4(\全加器_3_out_4 ));
  \全加器  \u_全加器_4  (.in_3(in_1[3]), .in_1(in_2[3]), .in_2(\全加器_3_out_4 ), .out_5(out_4[3]), .out_4(out_5));
endmodule

module \十六位全加器  (
  input  [15:0] in_1,
  input  [15:0] in_2,
  input  in_3,
  output [15:0] out_4,
  output out_5
);

  wire \四位全加器_1_out_5 , \四位全加器_2_out_5 , \四位全加器_3_out_5 ;

  \四位全加器  \u_四位全加器_1  (.in_1(in_1[3:0]), .in_2(in_2[3:0]), .in_3(in_3), .out_4(out_4[3:0]), .out_5(\四位全加器_1_out_5 ));
  \四位全加器  \u_四位全加器_2  (
    .in_1(in_1[7:4]), .in_2(in_2[7:4]), .in_3(\四位全加器_1_out_5 ), .out_4(out_4[7:4]), .out_5(\四位全加器_2_out_5 ));
  \四位全加器  \u_四位全加器_3  (
    .in_1(in_1[11:8]), .in_2(in_2[11:8]), .in_3(\四位全加器_2_out_5 ), .out_4(out_4[11:8]), .out_5(\四位全加器_3_out_5 ));
  \四位全加器  \u_四位全加器_4  (
    .in_1(in_1[15:12]), .in_2(in_2[15:12]), .in_3(\四位全加器_3_out_5 ), .out_4(out_4[15:12]), .out_5(out_5));
endmodule
