// Logisim project test6.circ as structural Verilog: 13 circuits, main circuit main
module main (
  input  Reset,
  output out_2,
  output [31:0] out_3,
  output [31:0] out_4,
  output [31:0] out_5,
  output out_6,
  output out_7,
  output out_8,
  output out_9,
  output [4:0] out_10,
  output [4:0] MemAddr,
  output [4:0] RegAddr,
  output [31:0] Instr
);

  wire AluSrc, and_5_out, and_6_out, and_7_out, and_8_out, and_9_out, and_10_out, and_11_out, B, BGEZ, BGTZ,
       BLEZ, BLTZ, BNE, Branch, BZ, clk, controller_1_regdst, controller_1_regwrite, div, divu, ExTOp, ifne,
       JALR, MemRead, MemtoReg1, MemtoReg2, MemtoReg3, MemtoReg4, MemtoReg5, MemtoReg6, MemtoReg7, MemtoReg8,
       MemtoReg9, MemtoReg10, mult, multu, my_xor, not_1_out, not_2_out, not_3_out, not_4_out, not_6_out,
       not_7_out, not_8_out, not_9_out, not_10_out, not_11_out, or_1_out, or_2_out, or_3_out, or_5_out,
       or_6_out, or_8_out, or_9_out, or_10_out, or_11_out, RegDst, sll_out, sllv_out, sra_out, srav_out,
       srl_out, srlv_out, sum_jump, xor_1_out, Zero, zero_ifne;
  wire [2:0] aluctrl, aluOp, multiplexer_7_out;
  wire [4:0] multiplexer_1_out;
  wire [7:0] multiplexer_19_out, RD2_7_0;
  wire [15:0] multiplexer_18_out, RD2_15_0;
  wire [27:0] bit_extender_3_out, shifter_1_out;
  wire [31:0] adder_2_out, Alu_high, Alu_out, bit_extender_2_out, bit_extender_4_out, bit_extender_5_out,
       bit_extender_10_out, bit_extender_11_out, data1, dm_1_rd, memword_q, multiplexer_4_out,
       multiplexer_5_out, multiplexer_6_out, multiplexer_8_out, multiplexer_9_out, multiplexer_10_out,
       multiplexer_11_out, multiplexer_12_out, multiplexer_13_out, multiplexer_14_out, multiplexer_16_out,
       multiplexer_17_out, multiplexer_20_out, multiplexer_23_out, multiplexer_24_out, multiplexer_25_out,
       multiplexer_26_out, multiplexer_27_out, multiplexer_28_out, multiplexer_30_out, multiplexer_31_out,
       multiplexer_32_out, multiplexer_34_out, multiplexer_35_out, multiplexer_36_out, multiplexer_37_out,
       multiplexer_38_out, not_5_out, pc_1_pc_out, RD2, RD_sb, RD_sh, shifter_2_out, shifter_6_out,
       shifter_8_out, sig_imm, sig_memword, sig_memword2, sllv_res, slti_res, sltiu_res, sra_res, srav_res,
       srlv_res, WD, yushu, zero_memword, zero_memword2;
  wire [32:0] zero_data1, zero_sig_imm;

  Clock clock_1 (.out(clk));
  IM im_1 (.A(out_10), .RD(Instr));
  Controller controller_1 (
    .opcode(Instr[31:26]), .AluSrc(AluSrc), .memToReg9(MemtoReg9), .regWrite(controller_1_regwrite),
    .BNE_out(BNE), .BZ_out(BZ), .BGTZ_out(BGTZ), .BLEZ_out(BLEZ), .memToReg10(MemtoReg10), .memRead(MemRead),
    .regDst(controller_1_regdst), .memWrite(out_8), .memToReg3(MemtoReg3), .extOp(ExTOp), .branch(Branch),
    .memToReg4(MemtoReg4), .aluOp(aluOp), .memToReg6(MemtoReg6), .memToReg8(MemtoReg8),
    .memToReg7(MemtoReg7), .memToReg({MemtoReg1, MemtoReg2}), .memToReg5(MemtoReg5), .Jump(out_6),
    .JAL_out(out_9));
  Multiplexer #(.width(5)) multiplexer_1 (
    .in0(Instr[20:16]), .in1(Instr[15:11]), .out(multiplexer_1_out), .sel(RegDst));
  not not_1 (not_1_out, div);
  not not_2 (not_2_out, divu);
  Multiplexer #(.width(5)) multiplexer_2 (.in0(multiplexer_1_out), .in1({5{1'b1}}), .out(RegAddr), .sel(out_9));
  and and_1 (out_2, not_1_out, controller_1_regwrite, not_2_out);
  not not_3 (not_3_out, div);
  not not_4 (not_4_out, divu);
  and and_2 (RegDst, not_3_out, not_4_out, controller_1_regdst);
  assign sig_imm = {{16{Instr[15]}}, Instr[15:0]};  // Bit_Extender bit_extender_1
  ALUCtrol aluctrol_1 (
    .func(Instr[5:0]), .aluOp(aluOp), .JR_out(out_7), .JALR_out(JALR), .multu_out(multu), .mult_out(mult),
    .divu_out(divu), .div_out(div), .sll_out(sll_out), .srl_out(srl_out), .sra_out(sra_out),
    .sllv_out(sllv_out), .srlv_out(srlv_out), .srav_out(srav_out), .xor_out(my_xor), .aluCtrl(aluctrl));
  Multiplexer #(.width(32)) multiplexer_3 (.in0(WD), .in1(not_5_out), .out(out_3), .sel(my_xor));
  assign bit_extender_2_out = {{16{1'b0}}, Instr[15:0]};  // Bit_Extender bit_extender_2
  assign bit_extender_3_out = {{2{1'b0}}, Instr[25:0]};  // Bit_Extender bit_extender_3
  GRF grf_1 (
    .WD(out_3), .RA1(Instr[25:21]), .WA(RegAddr), .Reset(Reset), .CLK(clk), .RA2(Instr[20:16]),
    .RegWrite(out_2), .RD1(data1), .RD2(RD2));
  assign not_5_out = ~WD;  // NOT_Gate not_5, 32 bits wide
  Multiplexer #(.width(32)) multiplexer_4 (
    .in0(sig_imm), .in1(bit_extender_2_out), .out(multiplexer_4_out), .sel(ExTOp));
  Shifter #(.width(28)) shifter_1 (.in(bit_extender_3_out), .\dist (5'b00010), .out(shifter_1_out));
  PC pc_1 (
    .PC_in(multiplexer_14_out), .CLK(clk), .Reset(Reset),
    .PC_out({pc_1_pc_out[31:7], out_10, pc_1_pc_out[1:0]}));
  BitSelector #(.group(8), .width(32)) bitselector_1 (.in(RD2), .out(RD2_7_0), .sel(2'b00));
  BitSelector #(.group(16), .width(32)) bitselector_2 (.in(RD2), .out(RD2_15_0), .sel(1'b0));
  Adder #(.width(32)) adder_1 (
    .a(32'h4), .b({pc_1_pc_out[31:7], out_10, pc_1_pc_out[1:0]}), .out(out_4));  // open: cin, cout
  Shifter #(.width(32)) shifter_2 (.in(multiplexer_4_out), .\dist (5'b00010), .out(shifter_2_out));
  Multiplexer #(.width(32)) multiplexer_5 (.in0(RD2), .in1(multiplexer_4_out), .out(multiplexer_5_out), .sel(AluSrc));
  assign bit_extender_4_out = {{1{1'b0}}, data1[30:0]};  // Bit_Extender bit_extender_4
  Multiplexer #(.width(32)) multiplexer_6 (.in0(multiplexer_5_out), .in1({32{1'b0}}), .out(multiplexer_6_out), .sel(B));
  Multiplexer #(.width(3)) multiplexer_7 (.in0(aluctrl), .in1(3'b000), .out(multiplexer_7_out), .sel(B));
  Adder #(.width(32)) adder_2 (.a(out_4), .b(shifter_2_out), .out(adder_2_out));  // open: cin, cout
  assign bit_extender_5_out = {{1{1'b0}}, RD2[30:0]};  // Bit_Extender bit_extender_5
  Multiplexer #(.width(32)) multiplexer_8 (
    .in0(data1), .in1(bit_extender_4_out), .out(multiplexer_8_out), .sel(or_1_out));
  or or_1 (or_1_out, mult, div);
  Multiplexer #(.width(32)) multiplexer_9 (
    .in0(multiplexer_6_out), .in1(bit_extender_5_out), .out(multiplexer_9_out), .sel(or_1_out));
  Multiplexer #(.width(32)) multiplexer_10 (.in0(out_4), .in1(adder_2_out), .out(multiplexer_10_out), .sel(sum_jump));
  Multiplexer #(.width(32)) multiplexer_11 (
    .in0(multiplexer_10_out), .in1({out_4[31:28], shifter_1_out}), .out(multiplexer_11_out), .sel(out_6));
  ALU alu_1 (
    .Data1(multiplexer_8_out), .Data2(multiplexer_9_out), .bne_in(BNE), .ALUStr(multiplexer_7_out),
    .Zero(Zero), .if_nega(ifne), .Outdata({Alu_out[31:7], MemAddr, Alu_out[1:0]}), .yushu(yushu),
    .high(Alu_high));
  Multiplexer #(.width(32)) multiplexer_12 (.in0(RD2), .in1(RD_sb), .out(multiplexer_12_out), .sel(MemtoReg7));
  Multiplexer #(.width(32)) multiplexer_13 (
    .in0(multiplexer_11_out), .in1(data1), .out(multiplexer_13_out), .sel(out_7));
  Multiplexer #(.width(32)) multiplexer_14 (
    .in0(multiplexer_13_out), .in1(data1), .out(multiplexer_14_out), .sel(JALR));
  or or_2 (or_2_out, Instr[16], Instr[17], Instr[18], Instr[19], Instr[20]);
  not not_6 (not_6_out, or_2_out);
  and and_3 (BLTZ, not_6_out, BZ);
  Multiplexer #(.width(32)) multiplexer_15 (.in0(multiplexer_12_out), .in1(RD_sh), .out(out_5), .sel(MemtoReg8));
  not not_7 (not_7_out, Instr[16]);
  or or_3 (or_3_out, not_7_out, Instr[17], Instr[18], Instr[19], Instr[20]);
  not not_8 (not_8_out, or_3_out);
  and and_4 (BGEZ, BZ, not_8_out);
  DM dm_1 (.Reset(Reset), .MemAddr(MemAddr), .MemWrite(out_8), .MemRead(MemRead), .clk(clk), .WD(out_5), .RD(dm_1_rd));
  not not_9 (not_9_out, Zero);
  not not_10 (not_10_out, data1[31]);
  and and_5 (and_5_out, not_9_out, BNE);
  Multiplexer #(.width(32)) multiplexer_16 (
    .in0({Alu_out[31:7], MemAddr, Alu_out[1:0]}), .in1(dm_1_rd), .out(multiplexer_16_out), .sel(MemtoReg1));
  and and_6 (and_6_out, Zero, Branch);
  Register #(.trigger("falling"), .width(32)) memword (.D(dm_1_rd), .en(1'b1), .clk(clk), .Q(memword_q), .clr(Reset));
  Multiplexer #(.width(32)) multiplexer_17 (
    .in0(multiplexer_16_out), .in1({Instr[15:0], {16{1'b0}}}), .out(multiplexer_17_out), .sel(MemtoReg2));
  and and_7 (and_7_out, BGTZ, not_10_out, not_9_out);
  or or_4 (sum_jump, and_5_out, and_6_out, and_7_out, and_8_out, and_9_out, and_10_out);
  Multiplexer #(.width(16)) multiplexer_18 (
    .in0(memword_q[15:0]), .in1(memword_q[31:16]), .out(multiplexer_18_out), .sel(MemAddr[1]));
  Multiplexer #(.select(2), .width(8)) multiplexer_19 (
    .in0(memword_q[7:0]), .in1(memword_q[15:8]), .in2(memword_q[23:16]), .in3(memword_q[31:24]),
    .out(multiplexer_19_out), .sel(MemAddr[1:0]));
  or or_5 (or_5_out, not_10_out, Zero);
  and and_8 (and_8_out, BGEZ, or_5_out);
  assign zero_memword2 = {{16{1'b0}}, multiplexer_18_out};  // Bit_Extender bit_extender_6
  assign sig_memword2 = {{16{multiplexer_18_out[15]}}, multiplexer_18_out};  // Bit_Extender bit_extender_7
  assign sig_memword = {{24{multiplexer_19_out[7]}}, multiplexer_19_out};  // Bit_Extender bit_extender_8
  assign zero_memword = {{24{1'b0}}, multiplexer_19_out};  // Bit_Extender bit_extender_9
  Multiplexer #(.width(32)) multiplexer_20 (
    .in0(multiplexer_17_out), .in1(sig_memword), .out(multiplexer_20_out), .sel(MemtoReg3));
  or or_6 (or_6_out, data1[31], Zero);
  and and_9 (and_9_out, BLEZ, or_6_out);
  Multiplexer #(.select(2), .width(32)) multiplexer_21 (
    .in0({dm_1_rd[31:8], RD2_7_0}), .in1({dm_1_rd[31:16], RD2_7_0, dm_1_rd[7:0]}),
    .in2({dm_1_rd[31:24], RD2_7_0, dm_1_rd[15:0]}), .in3({RD2_7_0, dm_1_rd[23:0]}), .out(RD_sb),
    .sel(MemAddr[1:0]));
  Multiplexer #(.width(32)) multiplexer_22 (
    .in0({dm_1_rd[31:16], RD2_15_0}), .in1({RD2_15_0, dm_1_rd[15:0]}), .out(RD_sh), .sel(MemAddr[1]));
  and and_10 (and_10_out, BLTZ, data1[31], not_9_out);
  Multiplexer #(.width(32)) multiplexer_23 (
    .in0(multiplexer_20_out), .in1(zero_memword), .out(multiplexer_23_out), .sel(MemtoReg4));
  Shifter #(.width(32)) shifter_3 (.in(RD2), .\dist (data1[4:0]), .out(sllv_res));
  Multiplexer #(.width(32)) multiplexer_24 (
    .in0(multiplexer_23_out), .in1(sig_memword2), .out(multiplexer_24_out), .sel(MemtoReg5));
  or or_7 (B, BGTZ, BGEZ, BLEZ, BLTZ);
  Shifter #(.shift("lr"), .width(32)) shifter_4 (.in(RD2), .\dist (data1[4:0]), .out(srlv_res));
  Shifter #(.shift("ar"), .width(32)) shifter_5 (.in(RD2), .\dist (data1[4:0]), .out(srav_res));
  Multiplexer #(.width(32)) multiplexer_25 (
    .in0(multiplexer_24_out), .in1(zero_memword2), .out(multiplexer_25_out), .sel(MemtoReg6));
  Multiplexer #(.width(32)) multiplexer_26 (
    .in0(multiplexer_25_out), .in1(out_4), .out(multiplexer_26_out), .sel(or_8_out));
  or or_8 (or_8_out, out_9, JALR);
  Multiplexer #(.width(32)) multiplexer_27 (.in0(yushu), .in1(Alu_high), .out(multiplexer_27_out), .sel(or_9_out));
  or or_9 (or_9_out, mult, multu);
  Multiplexer #(.width(32)) multiplexer_28 (
    .in0(multiplexer_26_out), .in1(slti_res), .out(multiplexer_28_out), .sel(MemtoReg9));
  Multiplexer #(.width(32)) multiplexer_29 (.in0({32{1'b0}}), .in1(32'h1), .out(sltiu_res), .sel(zero_ifne));
  assign bit_extender_10_out = {{1{1'b0}}, multiplexer_27_out[30:0]};  // Bit_Extender bit_extender_10
  assign bit_extender_11_out = {{1{1'b1}}, multiplexer_27_out[30:0]};  // Bit_Extender bit_extender_11
  Multiplexer #(.width(32)) multiplexer_30 (
    .in0(multiplexer_28_out), .in1(sltiu_res), .out(multiplexer_30_out), .sel(MemtoReg10));
  xor xor_1 (xor_1_out, data1[31], RD2[31]);
  or or_10 (or_10_out, div, mult);
  or or_11 (or_11_out, mult, div, multu, divu);
  Shifter #(.width(32)) shifter_6 (.in(RD2), .\dist (Instr[10:6]), .out(shifter_6_out));
  Multiplexer #(.width(32)) multiplexer_31 (
    .in0(bit_extender_10_out), .in1(bit_extender_11_out), .out(multiplexer_31_out), .sel(xor_1_out));
  Multiplexer #(.width(32)) multiplexer_32 (
    .in0(multiplexer_27_out), .in1(multiplexer_31_out), .out(multiplexer_32_out), .sel(or_10_out));
  Shifter #(.shift("ar"), .width(32)) shifter_7 (.in(RD2), .\dist (Instr[10:6]), .out(sra_res));
  Multiplexer #(.width(32)) multiplexer_33 (.in0({32{1'b0}}), .in1(32'h1), .out(slti_res), .sel(ifne));
  Multiplexer #(.width(32)) multiplexer_34 (
    .in0(multiplexer_30_out), .in1(shifter_6_out), .out(multiplexer_34_out), .sel(sll_out));
  Register #(.trigger("falling"), .width(32)) HI (
    .D(multiplexer_32_out), .en(or_11_out), .clk(clk), .clr(Reset));  // open: Q
  Register #(.trigger("falling"), .width(32)) LO (
    .D({Alu_out[31:7], MemAddr, Alu_out[1:0]}), .en(or_11_out), .clk(clk), .clr(Reset));  // open: Q
  Shifter #(.shift("lr"), .width(32)) shifter_8 (.in(RD2), .\dist (Instr[10:6]), .out(shifter_8_out));
  Multiplexer #(.width(32)) multiplexer_35 (
    .in0(multiplexer_34_out), .in1(shifter_8_out), .out(multiplexer_35_out), .sel(srl_out));
  Multiplexer #(.width(32)) multiplexer_36 (
    .in0(multiplexer_35_out), .in1(sra_res), .out(multiplexer_36_out), .sel(sra_out));
  assign zero_data1 = {{1{1'b0}}, data1};  // Bit_Extender bit_extender_12
  assign zero_sig_imm = {{1{1'b0}}, sig_imm};  // Bit_Extender bit_extender_13
  Multiplexer #(.width(32)) multiplexer_37 (
    .in0(multiplexer_36_out), .in1(sllv_res), .out(multiplexer_37_out), .sel(sllv_out));
  Multiplexer #(.width(32)) multiplexer_38 (
    .in0(multiplexer_37_out), .in1(srlv_res), .out(multiplexer_38_out), .sel(srlv_out));
  not not_11 (not_11_out, out_9);
  Subtractor #(.width(33)) subtractor_1 (.a(zero_data1), .b(zero_sig_imm), .bout(zero_ifne));  // open: out, bin
  Multiplexer #(.width(32)) multiplexer_39 (.in0(multiplexer_38_out), .in1(srav_res), .out(WD), .sel(and_11_out));
  and and_11 (and_11_out, not_11_out, srav_out);

  // Other names for the same wires on the sheet: PC_next[31:0] = out_4; IM_RD[31:0] = Instr;
  //   JumpAddr[25:0] = Instr[25:0]; s[4:0] = Instr[10:6]; Alu_out[6:2] = MemAddr; byte[1:0] = MemAddr[1:0];
  //   byte2 = MemAddr[1]; s2[4:0] = data1[4:0]; sign1 = data1[31]; JAL = out_9; JR = out_7; Jump = out_6;
  //   rt[4:0] = Instr[20:16]; MemData[31:0] = out_5; MemWrite = out_8; opcode[5:0] = Instr[31:26]; sign2 = RD2[31];
  //   RegData[31:0] = out_3; RegWrite = out_2
endmodule

module ALUCtrol (
  input  [5:0] func,
  input  [2:0] aluOp,
  output JR_out,
  output JALR_out,
  output multu_out,
  output mult_out,
  output divu_out,
  output div_out,
  output sll_out,
  output srl_out,
  output sra_out,
  output sllv_out,
  output srlv_out,
  output srav_out,
  output xor_out,
  output [2:0] aluCtrl
);

  wire addiu_out, addu_out, andi_out, beq_out, lb_out, lbu_out, lh_out, lhu_out, lui_out, lw_out, my_or_out,
       myand_out, mynor_out, not_1_out, not_2_out, not_3_out, not_4_out, not_5_out, not_6_out, not_7_out,
       not_8_out, not_9_out, one_out, or_2_out, ori_out, sb_out, sh_out, slti_out, subu_out, sw_out,
       xori_out, zero_out;

  not not_1 (not_1_out, aluOp[2]);
  not not_2 (not_2_out, aluOp[1]);
  not not_3 (not_3_out, aluOp[0]);
  not not_4 (not_4_out, func[5]);
  not not_5 (not_5_out, func[4]);
  not not_6 (not_6_out, func[3]);
  not not_7 (not_7_out, func[2]);
  not not_8 (not_8_out, func[1]);
  not not_9 (not_9_out, func[0]);
  and lw (lw_out, not_1_out, not_2_out, aluOp[0]);
  and sw (sw_out, not_1_out, not_2_out, aluOp[0]);
  and beq (beq_out, not_1_out, aluOp[1], not_3_out);
  and lui (lui_out, not_1_out, aluOp[1], aluOp[0]);
  and ori (ori_out, aluOp[2], aluOp[1], aluOp[0]);
  and addu (addu_out, not_1_out, not_2_out, not_3_out, func[5], not_5_out, not_6_out, not_7_out, not_8_out, func[0]);
  and subu (subu_out, not_1_out, not_2_out, not_3_out, func[5], not_5_out, not_6_out, not_7_out, func[1], func[0]);
  and lb (lb_out, not_1_out, not_2_out, aluOp[0]);
  and lbu (lbu_out, not_1_out, not_2_out, aluOp[0]);
  and lh (lh_out, not_1_out, not_2_out, aluOp[0]);
  and lhu (lhu_out, not_1_out, not_2_out, aluOp[0]);
  and sb (sb_out, not_1_out, not_2_out, aluOp[0]);
  and sh (sh_out, not_1_out, not_2_out, aluOp[0]);
  and JR (JR_out, not_4_out, not_5_out, func[3], not_7_out, not_8_out, not_9_out);
  and JALR (JALR_out, not_4_out, not_5_out, func[3], not_7_out, not_8_out, func[0]);
  and addiu (addiu_out, not_1_out, not_2_out, aluOp[0]);
  and andi (andi_out, aluOp[2], not_2_out, aluOp[0]);
  and xori (xori_out, aluOp[2], not_2_out, not_3_out);
  and slti (slti_out, aluOp[2], aluOp[1], not_3_out);
  and multu (multu_out, not_1_out, not_2_out, not_3_out, not_4_out, func[4], func[3], not_7_out, not_8_out, func[0]);
  and mult (mult_out, not_1_out, not_2_out, not_3_out, not_4_out, func[4], func[3], not_7_out, not_8_out, not_9_out);
  and divu (divu_out, not_1_out, not_2_out, not_3_out, not_4_out, func[4], func[3], not_7_out, func[1], func[0]);
  and div (div_out, not_1_out, not_2_out, not_3_out, not_4_out, func[4], func[3], not_7_out, func[1], not_9_out);
  and my_or (my_or_out, not_1_out, not_2_out, not_3_out, func[5], not_5_out, not_6_out, func[2], not_8_out, func[0]);
  and my_sll (sll_out, not_1_out, not_2_out, not_3_out, not_4_out, not_5_out, not_6_out, not_7_out, not_8_out, not_9_out);
  and my_srl (srl_out, not_1_out, not_2_out, not_3_out, not_4_out, not_5_out, not_6_out, not_7_out, func[1], not_9_out);
  and my_sra (sra_out, not_1_out, not_2_out, not_3_out, not_4_out, not_5_out, not_6_out, not_7_out, func[1], func[0]);
  and sllv (sllv_out, not_1_out, not_2_out, not_3_out, not_4_out, not_5_out, not_6_out, func[2], not_8_out, not_9_out);
  and srlv (srlv_out, not_1_out, not_2_out, not_3_out, not_4_out, not_5_out, not_6_out, func[2], func[1], not_9_out);
  and srav (srav_out, not_1_out, not_2_out, not_3_out, not_4_out, not_5_out, not_6_out, func[2], func[1], func[0]);
  and myand (myand_out, not_1_out, not_2_out, not_3_out, func[5], not_5_out, not_6_out, func[2], not_8_out, not_9_out);
  and myxor (xor_out, not_1_out, not_2_out, not_3_out, func[5], not_5_out, not_6_out, func[2], func[1], func[0]);
  and mynor (mynor_out, not_1_out, not_2_out, not_3_out, func[5], not_5_out, not_6_out, func[2], func[1], not_9_out);
  or or_1 (aluCtrl[2], mult_out, multu_out, or_2_out);
  or or_2 (or_2_out, andi_out, mynor_out, xori_out, myand_out, lui_out);
  or one (one_out, addiu_out, sb_out, lb_out, lbu_out, beq_out, lw_out, sw_out, addu_out, subu_out, lui_out, lh_out, lhu_out, sh_out, slti_out);
  or or_3 (aluCtrl[1], one_out, mult_out, multu_out);
  or zero (zero_out, xori_out, beq_out, ori_out, my_or_out, subu_out, lui_out, slti_out);
  or or_4 (aluCtrl[0], xor_out, mynor_out, zero_out);
endmodule

module Controller (
  input  [5:0] opcode,
  output AluSrc,
  output memToReg9,
  output regWrite,
  output BNE_out,
  output BZ_out,
  output BGTZ_out,
  output BLEZ_out,
  output memToReg10,
  output memRead,
  output regDst,
  output memWrite,
  output memToReg3,
  output extOp,
  output branch,
  output memToReg4,
  output [2:0] aluOp,
  output memToReg6,
  output memToReg8,
  output memToReg7,
  output [1:0] memToReg,
  output memToReg5,
  output Jump,
  output JAL_out
);

  wire addiu_out, alusrc_op, andi_out, J_out, not_1_out, not_2_out, not_3_out, not_4_out, not_5_out,
       not_6_out, ori_out, regwrite_op, sw_out, xori_out;

  not not_1 (not_1_out, opcode[5]);
  not not_2 (not_2_out, opcode[4]);
  not not_3 (not_3_out, opcode[3]);
  not not_4 (not_4_out, opcode[2]);
  not not_5 (not_5_out, opcode[1]);
  not not_6 (not_6_out, opcode[0]);
  and R (regDst, not_1_out, not_2_out, not_3_out, not_4_out, not_5_out, not_6_out);
  and lw (memToReg[1], opcode[5], not_2_out, not_3_out, not_4_out, opcode[1], opcode[0]);
  and sw (sw_out, opcode[5], not_2_out, opcode[3], not_4_out, opcode[1], opcode[0]);
  and beq (branch, not_1_out, not_2_out, not_3_out, opcode[2], not_5_out, not_6_out);
  and lui (memToReg[0], not_1_out, not_2_out, opcode[3], opcode[2], opcode[1], opcode[0]);
  and ori (ori_out, not_1_out, not_2_out, opcode[3], opcode[2], not_5_out, opcode[0]);
  and lb (memToReg3, opcode[5], not_2_out, not_3_out, not_4_out, not_5_out, not_6_out);
  and lbu (memToReg4, opcode[5], not_2_out, not_3_out, opcode[2], not_5_out, not_6_out);
  and lh (memToReg5, opcode[5], not_2_out, not_3_out, not_4_out, not_5_out, opcode[0]);
  and lhu (memToReg6, opcode[5], not_2_out, not_3_out, opcode[2], not_5_out, opcode[0]);
  and sb (memToReg7, opcode[5], not_2_out, opcode[3], not_4_out, not_5_out, not_6_out);
  and sh (memToReg8, opcode[5], not_2_out, opcode[3], not_4_out, not_5_out, opcode[0]);
  and J (J_out, not_1_out, not_2_out, not_3_out, not_4_out, opcode[1], not_6_out);
  and JAL (JAL_out, not_1_out, not_2_out, not_3_out, not_4_out, opcode[1], opcode[0]);
  and addiu (addiu_out, not_1_out, not_2_out, opcode[3], not_4_out, not_5_out, opcode[0]);
  and andi (andi_out, not_1_out, not_2_out, opcode[3], opcode[2], not_5_out, not_6_out);
  and xori (xori_out, not_1_out, not_2_out, opcode[3], opcode[2], opcode[1], not_6_out);
  and slti (memToReg9, not_1_out, not_2_out, opcode[3], not_4_out, opcode[1], not_6_out);
  and bne (BNE_out, not_1_out, not_2_out, not_3_out, opcode[2], not_5_out, opcode[0]);
  and bz (BZ_out, not_1_out, not_2_out, not_3_out, not_4_out, not_5_out, opcode[0]);
  and BGTZ (BGTZ_out, not_1_out, not_2_out, not_3_out, opcode[2], opcode[1], opcode[0]);
  and BLEZ (BLEZ_out, not_1_out, not_2_out, not_3_out, opcode[2], opcode[1], not_6_out);
  and sltiu (memToReg10, not_1_out, not_2_out, opcode[3], not_4_out, opcode[1], opcode[0]);
  or or_1 (alusrc_op, andi_out, memToReg8, memToReg6, memToReg4, memToReg[1], sw_out, memToReg3, ori_out, memToReg5, memToReg7, addiu_out, xori_out);
  or or_2 (regwrite_op, andi_out, JAL_out, memToReg5, memToReg3, regDst, memToReg[1], memToReg[0], ori_out, memToReg4, memToReg6, addiu_out, xori_out);
  or or_3 (memRead, memToReg6, memToReg[1], memToReg4, memToReg8, memToReg5, memToReg3, memToReg7);
  or or_4 (memWrite, sw_out, memToReg8, memToReg7);
  or or_5 (extOp, ori_out, xori_out, andi_out);
  or or_6 (aluOp[2], andi_out, xori_out, ori_out);
  or or_7 (aluOp[1], branch, memToReg[0], ori_out);
  or or_8 (aluOp[0], addiu_out, memToReg7, memToReg5, memToReg3, memToReg[1], sw_out, memToReg[0], ori_out, memToReg4, memToReg6, memToReg8, andi_out);
  or or_9 (Jump, JAL_out, J_out);
  or or_10 (AluSrc, alusrc_op, memToReg9);
  or or_11 (regWrite, regwrite_op, memToReg10, memToReg9);

  // Other names for the same wires on the sheet: slti = memToReg9; sltiu = memToReg10
endmodule

module IM (
  input  [4:0] A,
  output [31:0] RD
);

  ROM #(.addrWidth(5), .dataWidth(32)) rom_1 (.addr(A), .data(RD));
endmodule

module ALU (
  input  [31:0] Data1,
  input  [31:0] Data2,
  input  bne_in,
  input  [2:0] ALUStr,
  output Zero,
  output if_nega,
  output [31:0] Outdata,
  output [31:0] yushu,
  output [31:0] high
);

  wire or_2_out;
  wire [2:0] multiplexer_2_out;
  wire [31:0] and_1_out, divider_1_out, full_adder_32bit_1_sum, multiplier_1_out, or_1_out, subtractor_1_out,
       xor_1_out;

  Divider #(.width(32)) divider_1 (.a(Data1), .b(Data2), .out(divider_1_out), .rem(yushu));  // open: upper
  Subtractor #(.width(32)) subtractor_1 (.a(Data1), .b(Data2), .out(subtractor_1_out), .bout(if_nega));  // open: bin
  assign or_1_out = Data1 | Data2;  // OR_Gate or_1, 32 bits wide
  assign and_1_out = Data1 & Data2;  // AND_Gate and_1, 32 bits wide
  assign xor_1_out = Data1 ^ Data2;  // XOR_Gate xor_1, 32 bits wide
  full_adder_32bit full_adder_32bit_1 (.Ci_1(1'b0), .A(Data1), .B(Data2), .Sum(full_adder_32bit_1_sum));  // open: Ci
  Multiplier #(.width(32)) multiplier_1 (.a(Data1), .b(Data2), .out(multiplier_1_out), .cout(high));  // open: cin
  Multiplexer #(.select(3), .width(32)) multiplexer_1 (
    .in0(divider_1_out), .in1(or_1_out), .in2(full_adder_32bit_1_sum), .in3(subtractor_1_out),
    .in4(and_1_out), .in5(xor_1_out), .in6(multiplier_1_out), .in7(Data2), .out(Outdata),
    .sel(multiplexer_2_out));
  Multiplexer #(.width(3)) multiplexer_2 (.in0(ALUStr), .in1(3'b011), .out(multiplexer_2_out), .sel(bne_in));
  or or_2 (or_2_out, Outdata[0], Outdata[1], Outdata[2], Outdata[3], Outdata[4], Outdata[5], Outdata[6], Outdata[7], Outdata[8], Outdata[9], Outdata[10], Outdata[11], Outdata[12], Outdata[13], Outdata[14], Outdata[15], Outdata[16], Outdata[17], Outdata[18], Outdata[19], Outdata[20], Outdata[21], Outdata[22], Outdata[23], Outdata[24], Outdata[25], Outdata[26], Outdata[27], Outdata[28], Outdata[29], Outdata[30], Outdata[31]);
  not not_1 (Zero, or_2_out);
endmodule

module DM (
  input  Reset,
  input  [4:0] MemAddr,
  input  MemWrite,
  input  MemRead,
  input  clk,
  input  [31:0] WD,
  output [31:0] RD
);

  RAM #(.addrWidth(5), .asyncread("true"), .clearpin("true"), .dataWidth(32)) ram_1 (
    .addr(MemAddr), .we(MemWrite), .oe(MemRead), .clk(clk), .din(WD), .dout(RD), .clr(Reset));
endmodule

module GRF (
  input  [31:0] WD,
  input  [4:0] RA1,
  input  [4:0] WA,
  input  Reset,
  input  CLK,
  input  [4:0] RA2,
  input  RegWrite,
  output [31:0] RD1,
  output [31:0] RD2
);

  wire demultiplexer_2_out0, demultiplexer_2_out1, demultiplexer_2_out2, demultiplexer_2_out3,
       demultiplexer_2_out4, demultiplexer_2_out5, demultiplexer_2_out6, demultiplexer_2_out7,
       demultiplexer_2_out8, demultiplexer_2_out9, demultiplexer_2_out10, demultiplexer_2_out11,
       demultiplexer_2_out12, demultiplexer_2_out13, demultiplexer_2_out14, demultiplexer_2_out15,
       demultiplexer_2_out16, demultiplexer_2_out17, demultiplexer_2_out18, demultiplexer_2_out19,
       demultiplexer_2_out20, demultiplexer_2_out21, demultiplexer_2_out22, demultiplexer_2_out23,
       demultiplexer_2_out24, demultiplexer_2_out25, demultiplexer_2_out26, demultiplexer_2_out27,
       demultiplexer_2_out28, demultiplexer_2_out29, demultiplexer_2_out30, demultiplexer_2_out31;
  wire [31:0] demultiplexer_1_out0, demultiplexer_1_out1, demultiplexer_1_out2, demultiplexer_1_out3,
       demultiplexer_1_out4, demultiplexer_1_out5, demultiplexer_1_out6, demultiplexer_1_out7,
       demultiplexer_1_out8, demultiplexer_1_out9, demultiplexer_1_out10, demultiplexer_1_out11,
       demultiplexer_1_out12, demultiplexer_1_out13, demultiplexer_1_out14, demultiplexer_1_out15,
       demultiplexer_1_out16, demultiplexer_1_out17, demultiplexer_1_out18, demultiplexer_1_out19,
       demultiplexer_1_out20, demultiplexer_1_out21, demultiplexer_1_out22, demultiplexer_1_out23,
       demultiplexer_1_out24, demultiplexer_1_out25, demultiplexer_1_out26, demultiplexer_1_out27,
       demultiplexer_1_out28, demultiplexer_1_out29, demultiplexer_1_out30, demultiplexer_1_out31,
       register_1_q, register_2_q, register_3_q, register_4_q, register_5_q, register_6_q, register_7_q,
       register_8_q, register_9_q, register_10_q, register_11_q, register_12_q, register_13_q, register_14_q,
       register_15_q, register_16_q, register_17_q, register_18_q, register_19_q, register_20_q,
       register_21_q, register_22_q, register_23_q, register_24_q, register_25_q, register_26_q,
       register_27_q, register_28_q, register_29_q, Rg0_q, Rg7_q, Rg31_q;

  Demultiplexer #(.select(5), .width(32)) demultiplexer_1 (
    .out0(demultiplexer_1_out0), .out1(demultiplexer_1_out1), .out2(demultiplexer_1_out2),
    .out3(demultiplexer_1_out3), .out4(demultiplexer_1_out4), .out5(demultiplexer_1_out5),
    .out6(demultiplexer_1_out6), .out7(demultiplexer_1_out7), .out8(demultiplexer_1_out8),
    .out9(demultiplexer_1_out9), .out10(demultiplexer_1_out10), .out11(demultiplexer_1_out11),
    .out12(demultiplexer_1_out12), .out13(demultiplexer_1_out13), .out14(demultiplexer_1_out14),
    .out15(demultiplexer_1_out15), .out16(demultiplexer_1_out16), .out17(demultiplexer_1_out17),
    .out18(demultiplexer_1_out18), .out19(demultiplexer_1_out19), .out20(demultiplexer_1_out20),
    .out21(demultiplexer_1_out21), .out22(demultiplexer_1_out22), .out23(demultiplexer_1_out23),
    .out24(demultiplexer_1_out24), .out25(demultiplexer_1_out25), .out26(demultiplexer_1_out26),
    .out27(demultiplexer_1_out27), .out28(demultiplexer_1_out28), .out29(demultiplexer_1_out29),
    .out30(demultiplexer_1_out30), .out31(demultiplexer_1_out31), .in(WD), .sel(WA));
  Demultiplexer #(.select(5)) demultiplexer_2 (
    .out0(demultiplexer_2_out0), .out1(demultiplexer_2_out1), .out2(demultiplexer_2_out2),
    .out3(demultiplexer_2_out3), .out4(demultiplexer_2_out4), .out5(demultiplexer_2_out5),
    .out6(demultiplexer_2_out6), .out7(demultiplexer_2_out7), .out8(demultiplexer_2_out8),
    .out9(demultiplexer_2_out9), .out10(demultiplexer_2_out10), .out11(demultiplexer_2_out11),
    .out12(demultiplexer_2_out12), .out13(demultiplexer_2_out13), .out14(demultiplexer_2_out14),
    .out15(demultiplexer_2_out15), .out16(demultiplexer_2_out16), .out17(demultiplexer_2_out17),
    .out18(demultiplexer_2_out18), .out19(demultiplexer_2_out19), .out20(demultiplexer_2_out20),
    .out21(demultiplexer_2_out21), .out22(demultiplexer_2_out22), .out23(demultiplexer_2_out23),
    .out24(demultiplexer_2_out24), .out25(demultiplexer_2_out25), .out26(demultiplexer_2_out26),
    .out27(demultiplexer_2_out27), .out28(demultiplexer_2_out28), .out29(demultiplexer_2_out29),
    .out30(demultiplexer_2_out30), .out31(demultiplexer_2_out31), .in(RegWrite), .sel(WA));
  Register #(.width(32)) Rg0 (.D(demultiplexer_1_out0), .en(demultiplexer_2_out0), .clk(CLK), .Q(Rg0_q), .clr(Reset));
  Register #(.width(32)) register_1 (
    .D(demultiplexer_1_out8), .en(demultiplexer_2_out8), .clk(CLK), .Q(register_1_q), .clr(Reset));
  Register #(.width(32)) register_2 (
    .D(demultiplexer_1_out16), .en(demultiplexer_2_out16), .clk(CLK), .Q(register_2_q), .clr(Reset));
  Register #(.width(32)) register_3 (
    .D(demultiplexer_1_out24), .en(demultiplexer_2_out24), .clk(CLK), .Q(register_3_q), .clr(Reset));
  Register #(.width(32)) register_4 (
    .D(demultiplexer_1_out1), .en(demultiplexer_2_out1), .clk(CLK), .Q(register_4_q), .clr(Reset));
  Register #(.width(32)) register_5 (
    .D(demultiplexer_1_out9), .en(demultiplexer_2_out9), .clk(CLK), .Q(register_5_q), .clr(Reset));
  Register #(.width(32)) register_6 (
    .D(demultiplexer_1_out17), .en(demultiplexer_2_out17), .clk(CLK), .Q(register_6_q), .clr(Reset));
  Register #(.width(32)) register_7 (
    .D(demultiplexer_1_out25), .en(demultiplexer_2_out25), .clk(CLK), .Q(register_7_q), .clr(Reset));
  Register #(.width(32)) register_8 (
    .D(demultiplexer_1_out2), .en(demultiplexer_2_out2), .clk(CLK), .Q(register_8_q), .clr(Reset));
  Register #(.width(32)) register_9 (
    .D(demultiplexer_1_out10), .en(demultiplexer_2_out10), .clk(CLK), .Q(register_9_q), .clr(Reset));
  Register #(.width(32)) register_10 (
    .D(demultiplexer_1_out18), .en(demultiplexer_2_out18), .clk(CLK), .Q(register_10_q), .clr(Reset));
  Register #(.width(32)) register_11 (
    .D(demultiplexer_1_out26), .en(demultiplexer_2_out26), .clk(CLK), .Q(register_11_q), .clr(Reset));
  Register #(.width(32)) register_12 (
    .D(demultiplexer_1_out3), .en(demultiplexer_2_out3), .clk(CLK), .Q(register_12_q), .clr(Reset));
  Register #(.width(32)) register_13 (
    .D(demultiplexer_1_out11), .en(demultiplexer_2_out11), .clk(CLK), .Q(register_13_q), .clr(Reset));
  Register #(.width(32)) register_14 (
    .D(demultiplexer_1_out19), .en(demultiplexer_2_out19), .clk(CLK), .Q(register_14_q), .clr(Reset));
  Register #(.width(32)) register_15 (
    .D(demultiplexer_1_out27), .en(demultiplexer_2_out27), .clk(CLK), .Q(register_15_q), .clr(Reset));
  Register #(.width(32)) register_16 (
    .D(demultiplexer_1_out4), .en(demultiplexer_2_out4), .clk(CLK), .Q(register_16_q), .clr(Reset));
  Register #(.width(32)) register_17 (
    .D(demultiplexer_1_out12), .en(demultiplexer_2_out12), .clk(CLK), .Q(register_17_q), .clr(Reset));
  Register #(.width(32)) register_18 (
    .D(demultiplexer_1_out20), .en(demultiplexer_2_out20), .clk(CLK), .Q(register_18_q), .clr(Reset));
  Register #(.width(32)) register_19 (
    .D(demultiplexer_1_out28), .en(demultiplexer_2_out28), .clk(CLK), .Q(register_19_q), .clr(Reset));
  Register #(.width(32)) register_20 (
    .D(demultiplexer_1_out5), .en(demultiplexer_2_out5), .clk(CLK), .Q(register_20_q), .clr(Reset));
  Register #(.width(32)) register_21 (
    .D(demultiplexer_1_out13), .en(demultiplexer_2_out13), .clk(CLK), .Q(register_21_q), .clr(Reset));
  Register #(.width(32)) register_22 (
    .D(demultiplexer_1_out21), .en(demultiplexer_2_out21), .clk(CLK), .Q(register_22_q), .clr(Reset));
  Register #(.width(32)) register_23 (
    .D(demultiplexer_1_out29), .en(demultiplexer_2_out29), .clk(CLK), .Q(register_23_q), .clr(Reset));
  Register #(.width(32)) register_24 (
    .D(demultiplexer_1_out6), .en(demultiplexer_2_out6), .clk(CLK), .Q(register_24_q), .clr(Reset));
  Register #(.width(32)) register_25 (
    .D(demultiplexer_1_out14), .en(demultiplexer_2_out14), .clk(CLK), .Q(register_25_q), .clr(Reset));
  Register #(.width(32)) register_26 (
    .D(demultiplexer_1_out22), .en(demultiplexer_2_out22), .clk(CLK), .Q(register_26_q), .clr(Reset));
  Register #(.width(32)) register_27 (
    .D(demultiplexer_1_out30), .en(demultiplexer_2_out30), .clk(CLK), .Q(register_27_q), .clr(Reset));
  Register #(.width(32)) Rg7 (.D(demultiplexer_1_out7), .en(demultiplexer_2_out7), .clk(CLK), .Q(Rg7_q), .clr(Reset));
  Register #(.width(32)) register_28 (
    .D(demultiplexer_1_out15), .en(demultiplexer_2_out15), .clk(CLK), .Q(register_28_q), .clr(Reset));
  Register #(.width(32)) register_29 (
    .D(demultiplexer_1_out23), .en(demultiplexer_2_out23), .clk(CLK), .Q(register_29_q), .clr(Reset));
  Register #(.width(32)) Rg31 (
    .D(demultiplexer_1_out31), .en(demultiplexer_2_out31), .clk(CLK), .Q(Rg31_q), .clr(Reset));
  Multiplexer #(.select(5), .width(32)) multiplexer_1 (
    .in0(Rg0_q), .in1(register_4_q), .in2(register_8_q), .in3(register_12_q), .in4(register_16_q),
    .in5(register_20_q), .in6(register_24_q), .in7(Rg7_q), .in8(register_1_q), .in9(register_5_q),
    .in10(register_9_q), .in11(register_13_q), .in12(register_17_q), .in13(register_21_q),
    .in14(register_25_q), .in15(register_28_q), .in16(register_2_q), .in17(register_6_q),
    .in18(register_10_q), .in19(register_14_q), .in20(register_18_q), .in21(register_22_q),
    .in22(register_26_q), .in23(register_29_q), .in24(register_3_q), .in25(register_7_q),
    .in26(register_11_q), .in27(register_15_q), .in28(register_19_q), .in29(register_23_q),
    .in30(register_27_q), .in31(Rg31_q), .out(RD1), .sel(RA1));
  Multiplexer #(.select(5), .width(32)) multiplexer_2 (
    .in0(Rg0_q), .in1(register_4_q), .in2(register_8_q), .in3(register_12_q), .in4(register_16_q),
    .in5(register_20_q), .in6(register_24_q), .in7(Rg7_q), .in8(register_1_q), .in9(register_5_q),
    .in10(register_9_q), .in11(register_13_q), .in12(register_17_q), .in13(register_21_q),
    .in14(register_25_q), .in15(register_28_q), .in16(register_2_q), .in17(register_6_q),
    .in18(register_10_q), .in19(register_14_q), .in20(register_18_q), .in21(register_22_q),
    .in22(register_26_q), .in23(register_29_q), .in24(register_3_q), .in25(register_7_q),
    .in26(register_11_q), .in27(register_15_q), .in28(register_19_q), .in29(register_23_q),
    .in30(register_27_q), .in31(Rg31_q), .out(RD2), .sel(RA2));
endmodule

module PC (
  input  [31:0] PC_in,
  input  CLK,
  input  Reset,
  output [31:0] PC_out
);

  Register #(.width(32)) register_1 (.D(PC_in), .en(1'b1), .clk(CLK), .Q(PC_out), .clr(Reset));
endmodule

module half_adder (
  input  A,
  input  B,
  output Sum,
  output Cout
);

  xor xor_1 (Sum, A, B);
  and and_1 (Cout, A, B);
endmodule

module full_adder_1bit (
  input  Ci_1,
  input  A,
  input  B,
  output Sum,
  output Ci
);

  wire half_adder_1_cout, half_adder_1_sum, half_adder_2_cout;

  half_adder half_adder_1 (.A(A), .B(B), .Sum(half_adder_1_sum), .Cout(half_adder_1_cout));
  half_adder half_adder_2 (.A(Ci_1), .B(half_adder_1_sum), .Sum(Sum), .Cout(half_adder_2_cout));
  or or_1 (Ci, half_adder_2_cout, half_adder_1_cout);
endmodule

module full_adder_4bit (
  input  Ci_1,
  input  [3:0] A,
  input  [3:0] B,
  output [3:0] Sum,
  output Ci
);

  wire full_adder_1bit_1_ci, full_adder_1bit_2_ci, full_adder_1bit_3_ci;

  full_adder_1bit full_adder_1bit_1 (.Ci_1(Ci_1), .A(A[0]), .B(B[0]), .Sum(Sum[0]), .Ci(full_adder_1bit_1_ci));
  full_adder_1bit full_adder_1bit_2 (
    .Ci_1(full_adder_1bit_1_ci), .A(A[1]), .B(B[1]), .Sum(Sum[1]), .Ci(full_adder_1bit_2_ci));
  full_adder_1bit full_adder_1bit_3 (
    .Ci_1(full_adder_1bit_2_ci), .A(A[2]), .B(B[2]), .Sum(Sum[2]), .Ci(full_adder_1bit_3_ci));
  full_adder_1bit full_adder_1bit_4 (.Ci_1(full_adder_1bit_3_ci), .A(A[3]), .B(B[3]), .Sum(Sum[3]), .Ci(Ci));
endmodule

module full_adder_16bit (
  input  Ci_1,
  input  [15:0] A,
  input  [15:0] B,
  output [15:0] Sum,
  output Ci
);

  wire full_adder_4bit_1_ci, full_adder_4bit_2_ci, full_adder_4bit_3_ci;

  full_adder_4bit full_adder_4bit_1 (.Ci_1(Ci_1), .A(A[3:0]), .B(B[3:0]), .Sum(Sum[3:0]), .Ci(full_adder_4bit_1_ci));
  full_adder_4bit full_adder_4bit_2 (
    .Ci_1(full_adder_4bit_1_ci), .A(A[7:4]), .B(B[7:4]), .Sum(Sum[7:4]), .Ci(full_adder_4bit_2_ci));
  full_adder_4bit full_adder_4bit_3 (
    .Ci_1(full_adder_4bit_2_ci), .A(A[11:8]), .B(B[11:8]), .Sum(Sum[11:8]), .Ci(full_adder_4bit_3_ci));
  full_adder_4bit full_adder_4bit_4 (
    .Ci_1(full_adder_4bit_3_ci), .A(A[15:12]), .B(B[15:12]), .Sum(Sum[15:12]), .Ci(Ci));
endmodule

module full_adder_32bit (
  input  Ci_1,
  input  [31:0] A,
  input  [31:0] B,
  output [31:0] Sum,
  output Ci
);

  wire full_adder_16bit_1_ci;

  full_adder_16bit full_adder_16bit_1 (
    .Ci_1(Ci_1), .A(A[15:0]), .B(B[15:0]), .Sum(Sum[15:0]), .Ci(full_adder_16bit_1_ci));
  full_adder_16bit full_adder_16bit_2 (
    .Ci_1(full_adder_16bit_1_ci), .A(A[31:16]), .B(B[31:16]), .Sum(Sum[31:16]), .Ci(Ci));
endmodule
